// Logisim project ALU.circ as structural Verilog: 3 circuits, main circuit ALU main
module ALU_main (
  input  [31:0] Rs,
  input  [31:0] Rt,
  input  [3:0] Select_Op,
  input  Hight_Op,
  input  Unsigned,
  output [31:0] Shoosed,
  output [31:0] Hight,
  output Great,
  output Equal,
  output Less,
  output C_Add,
  output C_Rest,
  output Div_x_0
);

  wire LessU, OpHight;
  wire [31:0] ADD, AND, DIV, Div_t, Divu, Mult, multiplexer_3_out, multiplexer_4_out, Mulu, NOR, OR, R_Div,
       R_Divu, R_Mult, R_Mulu, Slt, Sltu, SUB, XOR;

  assign AND = Rs & Rt;  // AND_Gate and_1, 32 bits wide
  assign OR = Rs | Rt;  // OR_Gate or_1, 32 bits wide
  assign XOR = Rs ^ Rt;  // XOR_Gate xor_1, 32 bits wide
  assign NOR = ~(Rs | Rt);  // NOR_Gate nor_1, 32 bits wide
  Adder #(.width(32)) adder_1 (.a(Rs), .b(Rt), .out(ADD), .cin(1'b0), .cout(C_Add));
  Subtractor #(.width(32)) subtractor_1 (.a(Rs), .b(Rt), .out(SUB), .bin(1'b0), .bout(C_Rest));
  Divu divu_1 (.Rs(Rs), .Lo(Divu), .Hi(R_Divu), .Rt(Rt));
  Comparator #(.width(32)) comparator_1 (.a(Rs), .b(Rt), .gt(Great), .eq(Equal), .lt(Less));
  Multiplexer #(.width(32), .enable("false")) multiplexer_1 (.in0({32{1'b0}}), .in1(32'h1), .out(Slt), .sel(Less));
  Multiplier #(.width(32)) multiplier_1 (.a(Rs), .b(Rt), .out(Mult), .cin({32{1'b0}}), .cout(R_Mult));
  Divider #(.width(32)) divider_1 (.a(Rs), .b(Rt), .out(DIV), .upper({32{1'b0}}), .rem(R_Div));
  Mulu mulu_1 (.Rs(Rs), .Lo(Mulu), .Hi(R_Mulu), .Rt(Rt));
  Comparator #(.width(32), .mode("unsigned")) comparator_2 (.a(Rs), .b(Rt), .lt(LessU));  // open: gt, eq
  Multiplexer #(.width(32), .enable("false")) multiplexer_2 (.in0({32{1'b0}}), .in1(32'h1), .out(Sltu), .sel(LessU));
  Multiplexer #(.width(32), .enable("false")) multiplexer_3 (
    .in0(R_Mult), .in1(R_Mulu), .out(multiplexer_3_out), .sel(Unsigned));
  Multiplexer #(.width(32), .enable("false")) multiplexer_4 (
    .in0(R_Div), .in1(R_Divu), .out(multiplexer_4_out), .sel(Unsigned));
  Multiplexer #(.select(4), .width(32), .enable("false")) multiplexer_5 (
    .in0(ADD), .in1(SUB), .in2(Mult), .in3(Mulu), .in4(Divu), .in5(Div_t), .in6(AND), .in7(OR), .in8(NOR),
    .in9(XOR), .in10(Slt), .in11(Sltu), .out(Shoosed), .sel(Select_Op));  // open: in12, in13, in14, in15
  Multiplexer #(.width(32), .enable("false")) multiplexer_6 (
    .in0(multiplexer_3_out), .in1(multiplexer_4_out), .out(Hight), .sel(OpHight));
  Comparator #(.width(32), .mode("unsigned")) comparator_3 (.a(Rt), .b({32{1'b0}}), .eq(Div_x_0));  // open: gt, lt

  // Other names for the same wires on the sheet: A[31:0] = Rs; B[31:0] = Rt; D0 = Div_x_0; Hi_S[31:0] = Hight;
  //   OpHight_t = Hight_Op

  // Notes on the sheet:
  //   Entradas
  //   Logical Operations
  //   Comparers
  //   Aritmetic Operations
  //   General Shooser
  //   Hight Shooser
  //   Cero Div
  //   Exits
  //   Flags
endmodule

module Mulu (
  input  [31:0] Rs,
  input  [31:0] Rt,
  output [31:0] Lo,
  output [31:0] Hi
);

  wire [31:0] adder_1_out, multiplexer_1_out, multiplexer_2_out, multiplier_1_cout;

  Multiplexer #(.width(32), .enable("false")) multiplexer_1 (
    .in0({32{1'b0}}), .in1(Rs), .out(multiplexer_1_out), .sel(Rt[31]));
  Multiplexer #(.width(32), .enable("false")) multiplexer_2 (
    .in0({32{1'b0}}), .in1(Rt), .out(multiplexer_2_out), .sel(Rs[31]));
  Adder #(.width(32)) adder_1 (
    .a(multiplexer_1_out), .b(multiplexer_2_out), .out(adder_1_out), .cin(1'b0));  // open: cout
  Multiplier #(.width(32)) multiplier_1 (.a(Rs), .b(Rt), .out(Lo), .cin({32{1'b0}}), .cout(multiplier_1_cout));
  Adder #(.width(32)) adder_2 (.a(multiplier_1_cout), .b(adder_1_out), .out(Hi), .cin(1'b0));  // open: cout

  // Other names for the same wires on the sheet: A[31:0] = Rs; B[31:0] = Rt
endmodule

module Divu (
  input  [31:0] Rs,
  input  [31:0] Rt,
  output [31:0] Lo,
  output [31:0] Hi
);

  wire xor_1_out;
  wire [31:0] divider_1_out, multiplexer_1_out, multiplexer_2_out, negator_1_out, negator_2_out,
       negator_3_out;

  Negator #(.width(32)) negator_1 (.in(Rs), .out(negator_1_out));
  Negator #(.width(32)) negator_2 (.in(Rt), .out(negator_2_out));
  Multiplexer #(.width(32), .enable("false")) multiplexer_1 (
    .in0(Rs), .in1(negator_1_out), .out(multiplexer_1_out), .sel(Rs[31]));
  Multiplexer #(.width(32), .enable("false")) multiplexer_2 (
    .in0(Rt), .in1(negator_2_out), .out(multiplexer_2_out), .sel(Rt[31]));
  Divider #(.width(32)) divider_1 (
    .a(multiplexer_1_out), .b(multiplexer_2_out), .out(divider_1_out), .rem(Hi));  // open: upper
  xor xor_1 (xor_1_out, Rs[31], Rt[31]);
  Negator #(.width(32)) negator_3 (.in(divider_1_out), .out(negator_3_out));
  Multiplexer #(.width(32), .enable("false")) multiplexer_3 (
    .in0(divider_1_out), .in1(negator_3_out), .out(Lo), .sel(xor_1_out));
endmodule
