// Logisim project Branch_Control.circ as structural Verilog: 3 circuits, main circuit Branch Constructor
module Branch_Control (
  input  [31:0] PC_in,
  input  [15:0] \const ,
  input  [31:0] Rs,
  input  Branche,
  input  Jump_Op,
  input  [25:0] Jump,
  input  jr,
  output [31:0] PC_Out
);

  wire [1:0] special_encoder_1_out_4;
  wire [31:0] bit_extender_1_out, Branch, jump_t, Standart;

  Special_encoder special_encoder_1 (.in_1(Branche), .in_2(Jump_Op), .in_3(jr), .out_4(special_encoder_1_out_4));
  Multiplexer #(.select(2), .width(32)) multiplexer_1 (
    .in0(Standart), .in1(Branch), .in2(jump_t), .in3(Rs), .out(PC_Out), .sel(special_encoder_1_out_4));  // open: en
  Adder #(.width(32)) adder_1 (.a(PC_in), .b(32'h4), .out(Standart));  // open: cin, cout
  assign bit_extender_1_out = {{16{\const [15]}}, \const };  // Bit_Extender bit_extender_1
  Branch_Constructor branch_constructor_1 (.Jump(Jump), .PC(PC_in), .Out(jump_t));
  Adder #(.width(32)) adder_2 (.a(Standart), .b(bit_extender_1_out), .out(Branch));  // open: cin, cout

  // Notes on the sheet:
  //   Choose PC Value
  //   Standart Value
  //   Branch Value
  //   Jump Value
endmodule

module Branch_Constructor (
  input  [25:0] Jump,
  input  [31:0] PC,
  output [31:0] Out
);


  assign Out = {PC[31:28], Jump, 2'b00};
endmodule

module Special_encoder (
  input  in_1,
  input  in_2,
  input  in_3,
  output [1:0] out_4
);

  wire and_1_out, and_2_out, and_3_out;

  and and_1 (and_1_out, in_1, ~in_2, ~in_3);  // AND_Gate
  and and_2 (and_2_out, ~in_1, ~in_2, in_3);  // AND_Gate
  and and_3 (and_3_out, ~in_1, in_2, ~in_3);  // AND_Gate
  or or_1 (out_4[0], and_1_out, and_2_out);
  or or_2 (out_4[1], and_2_out, and_3_out);
endmodule
