// Logisim project Data Path.circ as structural Verilog
module Little_Endian_Inmput (
  input  [31:0] in_1,
  output [31:0] out_2
);


  assign out_2 = in_1;
endmodule

module Branch_Control (
  input  [31:0] Rs,
  input  [2:0] Branch_Operation,
  input  Rs_____Rt,
  input  [31:0] PC_in,
  input  [15:0] \const ,
  input  [25:0] Jump,
  output [31:0] PC_Out
);

  wire and_1_out, and_2_out, and_3_out, and_4_out, and_5_out, b_jump, beq, bgtz, blez, bltz, bne,
       comparator_1_eq, comparator_1_lt, j, jr, nop, Rs____0, Rs_____0;
  wire [1:0] jump_t;
  wire [2:0] Branch_Ope;
  wire [25:0] Destiny_Jump;
  wire [31:0] bit_extender_1_out, Branch, jump_c, PC, Standart;
  wire [31:28] J_PC;

  Decoder #(.select(3), .disabled(0), .enable("false")) decoder_1 (
    .out0(nop), .out1(beq), .out2(bne), .out3(blez), .out4(bgtz), .out5(bltz), .out6(j), .out7(jr),
    .sel(Branch_Ope));
  Multiplexer #(.select(2), .width(32), .disabled(0), .enable("false")) multiplexer_1 (
    .in0(Standart), .in1(Branch), .in2({J_PC, Destiny_Jump, 2'b00}), .in3(Rs), .out(PC_Out), .sel(jump_t));
  Adder #(.width(32)) adder_1 (.a(PC_in), .b(32'h4), .out(Standart));  // open: cin, cout
  assign bit_extender_1_out = {{16{\const [15]}}, \const };  // Bit_Extender bit_extender_1
  BitSelector #(.width(32), .group(4)) bitselector_1 (.in(PC), .out(J_PC), .sel(3'b111));
  Branch_Constructor branch_constructor_1 (.Jump(Jump), .PC(PC_in), .Out(jump_c));
  Adder #(.width(32)) adder_2 (.a(Standart), .b(bit_extender_1_out), .out(Branch));  // open: cin, cout
  Comparator #(.width(32)) comparator_1 (
    .a(Rs), .b({32{1'b0}}), .eq(comparator_1_eq), .lt(comparator_1_lt));  // open: gt
  Comparator #(.width(32)) comparator_2 (.a(Rs), .b({32{1'b0}}), .lt(Rs____0));  // open: gt, eq
  and and_1 (and_1_out, beq, Rs_____Rt);
  and and_2 (and_2_out, bne, ~Rs_____Rt);  // AND_Gate
  and and_3 (and_3_out, blez, Rs_____0);
  and and_4 (and_4_out, bgtz, ~Rs_____0);  // AND_Gate
  and and_5 (and_5_out, bltz, Rs____0);
  or or_1 (Rs_____0, comparator_1_eq, comparator_1_lt);
  or or_2 (b_jump, and_1_out, and_2_out, and_3_out, and_4_out, and_5_out);
  Priority_Encoder #(.select(2)) priority_encoder_1 (
    .in0(nop), .in1(b_jump), .in2(j), .in3(jr), .out(jump_t), .en_in(1'b1));  // open: gs, en_out

  // Other names for the same wires on the sheet: Branch_Ope_t[2:0] = Branch_Operation; J_PC[27:2] = Destiny_Jump

  // Notes on the sheet:
  //   Ope Decode
  //   Output
  //   Standart Value
  //   Branch Value
  //   Jump Value
  //   J Jump 
  //   Jump Encode
endmodule

module Register_File (
  input  CLCK,
  input  [31:0] Dato_de_Entrada,
  input  RESET,
  input  En_SP,
  input  pop,
  input  [31:0] High,
  input  [31:0] Low,
  input  [4:0] SA,
  input  H_L_Enable,
  input  [4:0] SB,
  input  Enable,
  input  [4:0] Register_Address,
  output [31:0] Salida_High,
  output [31:0] Salida_Low,
  output [31:0] Salida_B,
  output [31:0] Salida_A,
  output [31:0] SP
);

  wire or_1_out, R1, R2, R3, R4, R5, R6, R7, R8, R9, R10, R11, R12, R13, R14, R15, R16, R17, R18, R19, R20,
       R21, R22, R23, R24, R25, R26, R27, R28, R29, R30, R31;
  wire [31:0] adder_1_out, DI, multiplexer_2_out, S0, S1, S2, S3, S4, S5, S6, S7, S8, S9, S10, S11, S12, S13,
       S14, S15, S16, S17, S18, S19, S20, S21, S22, S23, S24, S25, S26, S27, S28, S29, S30, S31, SP_t,
       subtractor_1_out;

  Demultiplexer #(.select(5), .enable("false")) demultiplexer_1 (
    .out0(R1), .out1(R2), .out2(R3), .out3(R4), .out4(R5), .out5(R6), .out6(R7), .out7(R8), .out8(R9),
    .out9(R10), .out10(R11), .out11(R12), .out12(R13), .out13(R14), .out14(R15), .out15(R16), .out16(R16),
    .out17(R17), .out18(R18), .out19(R19), .out20(R20), .out21(R21), .out22(R22), .out23(R23), .out24(R24),
    .out25(R25), .out26(R26), .out27(R27), .out28(R28), .out29(R29), .out30(R30), .out31(R31), .in(Enable),
    .sel(Register_Address));
  Register #(.width(32)) register_1 (.Q(S0));  // open: D, en, clk, clr
  Register #(.width(32)) register_2 (.D(Dato_de_Entrada), .en(R8), .Q(S8), .clk(CLCK), .clr(RESET));
  Register #(.width(32)) register_3 (.D(Dato_de_Entrada), .en(R16), .Q(S16), .clk(CLCK), .clr(RESET));
  Register #(.width(32)) register_4 (.D(Dato_de_Entrada), .en(R24), .Q(S24), .clk(CLCK), .clr(RESET));
  Register #(.width(32)) register_5 (.D(Dato_de_Entrada), .en(R1), .Q(S1), .clk(CLCK), .clr(RESET));
  Register #(.width(32)) register_6 (.D(Dato_de_Entrada), .en(R9), .Q(S9), .clk(CLCK), .clr(RESET));
  Register #(.width(32)) register_7 (.D(Dato_de_Entrada), .en(R17), .Q(S17), .clk(CLCK), .clr(RESET));
  Register #(.width(32)) register_8 (.D(Dato_de_Entrada), .en(R25), .Q(S25), .clk(CLCK), .clr(RESET));
  Register #(.width(32)) register_9 (.D(Dato_de_Entrada), .en(R2), .Q(S2), .clk(CLCK), .clr(RESET));
  Register #(.width(32)) register_10 (.D(Dato_de_Entrada), .en(R10), .Q(S10), .clk(CLCK), .clr(RESET));
  Register #(.width(32)) register_11 (.D(Dato_de_Entrada), .en(R18), .Q(S18), .clk(CLCK), .clr(RESET));
  Register #(.width(32)) register_12 (.D(Dato_de_Entrada), .en(R26), .Q(S26), .clk(CLCK), .clr(RESET));
  Register #(.width(32)) register_13 (.D(Dato_de_Entrada), .en(R3), .Q(S3), .clk(CLCK), .clr(RESET));
  Register #(.width(32)) register_14 (.D(Dato_de_Entrada), .en(R11), .Q(S11), .clk(CLCK), .clr(RESET));
  Register #(.width(32)) register_15 (.D(Dato_de_Entrada), .en(R19), .Q(S19), .clk(CLCK), .clr(RESET));
  Register #(.width(32)) register_16 (.D(Dato_de_Entrada), .en(R27), .Q(S27), .clk(CLCK), .clr(RESET));
  Register #(.width(32)) register_17 (.D(Dato_de_Entrada), .en(R4), .Q(S4), .clk(CLCK), .clr(RESET));
  Register #(.width(32)) register_18 (.D(Dato_de_Entrada), .en(R12), .Q(S12), .clk(CLCK), .clr(RESET));
  Register #(.width(32)) register_19 (.D(Dato_de_Entrada), .en(R20), .Q(S20), .clk(CLCK), .clr(RESET));
  Register #(.width(32)) register_20 (.D(Dato_de_Entrada), .en(R28), .Q(S28), .clk(CLCK), .clr(RESET));
  Subtractor #(.width(32)) subtractor_1 (.a(SP), .b(32'h4), .out(subtractor_1_out));  // open: bin, bout
  Multiplexer #(.width(32), .disabled(0), .enable("false")) multiplexer_1 (
    .in0(subtractor_1_out), .in1(adder_1_out), .out(SP_t), .sel(pop));
  Adder #(.width(32)) adder_1 (.a(SP), .b(32'h4), .out(adder_1_out));  // open: cin, cout
  Register #(.width(32)) register_21 (.D(Dato_de_Entrada), .en(R5), .Q(S5), .clk(CLCK), .clr(RESET));
  Register #(.width(32)) register_22 (.D(Dato_de_Entrada), .en(R13), .Q(S13), .clk(CLCK), .clr(RESET));
  Register #(.width(32)) register_23 (.D(Dato_de_Entrada), .en(R21), .Q(S21), .clk(CLCK), .clr(RESET));
  Register #(.width(32)) register_24 (.D(Dato_de_Entrada), .en(R29), .Q(S29), .clk(CLCK), .clr(RESET));
  Register #(.width(32)) register_25 (.D(Dato_de_Entrada), .en(R6), .Q(S6), .clk(CLCK), .clr(RESET));
  Multiplexer #(.width(32), .disabled(0), .enable("false")) multiplexer_2 (
    .in0(DI), .in1(SP_t), .out(multiplexer_2_out), .sel(En_SP));
  Register #(.width(32)) register_26 (.D(Dato_de_Entrada), .en(R14), .Q(S14), .clk(CLCK), .clr(RESET));
  Register #(.width(32)) register_27 (.D(Dato_de_Entrada), .en(R22), .Q(S22), .clk(CLCK), .clr(RESET));
  Register #(.width(32)) register_28 (.D(Dato_de_Entrada), .en(R30), .Q(S30), .clk(CLCK), .clr(RESET));
  Multiplexer #(.select(5), .width(32), .enable("false")) multiplexer_3 (
    .in0(S0), .in1(S1), .in2(S2), .in3(S3), .in4(S4), .in5(S5), .in6(S6), .in7(S7), .in8(S8), .in9(S9),
    .in10(S10), .in11(S11), .in12(S12), .in13(S13), .in14(S14), .in15(S15), .in16(S16), .in17(S17),
    .in18(S18), .in19(S19), .in20(S20), .in21(S21), .in22(S22), .in23(S23), .in24(S24), .in25(S25),
    .in26(S26), .in27(S27), .in28(S28), .in29(S29), .in30(S30), .in31(S31), .out(Salida_A), .sel(SA));
  Register #(.width(32)) u_SP (.D(multiplexer_2_out), .en(or_1_out), .Q(SP), .clk(CLCK), .clr(RESET));
  or or_1 (or_1_out, En_SP, R31);
  Register #(.width(32)) register_29 (.D(Dato_de_Entrada), .en(R7), .Q(S7), .clk(CLCK), .clr(RESET));
  Register #(.width(32)) register_30 (.D(Dato_de_Entrada), .en(R15), .Q(S15), .clk(CLCK), .clr(RESET));
  Register #(.width(32)) register_31 (.D(Dato_de_Entrada), .en(R23), .Q(S23), .clk(CLCK), .clr(RESET));
  Register #(.width(32)) register_32 (.D(Dato_de_Entrada), .en(R31), .Q(S31), .clk(CLCK), .clr(RESET));
  Register #(.width(32)) register_33 (.D(High), .en(H_L_Enable), .Q(Salida_High), .clk(CLCK), .clr(RESET));
  Register #(.width(32)) register_34 (.D(Low), .en(H_L_Enable), .Q(Salida_Low), .clk(CLCK), .clr(RESET));
  Multiplexer #(.select(5), .width(32), .enable("false")) multiplexer_4 (
    .in0(S0), .in1(S1), .in2(S2), .in3(S3), .in4(S4), .in5(S5), .in6(S6), .in7(S7), .in8(S8), .in9(S9),
    .in10(S10), .in11(S11), .in12(S12), .in13(S13), .in14(S14), .in15(S15), .in16(S16), .in17(S17),
    .in18(S18), .in19(S19), .in20(S20), .in21(S21), .in22(S22), .in23(S23), .in24(S24), .in25(S25),
    .in26(S26), .in27(S27), .in28(S28), .in29(S29), .in30(S30), .in31(S31), .out(Salida_B), .sel(SB));

  // Other names for the same wires on the sheet: Clock = CLCK; DE[31:0] = Dato_de_Entrada; H[31:0] = Salida_High;
  //   H_L = H_L_Enable; L[31:0] = Salida_Low; QSP[31:0] = SP

  // Notes on the sheet:
  //   Selector A
  //   Selector B
  //   Data SP
endmodule

module Data_Path (
  input  [31:0] Bank_0,
  input  [31:0] Bank_1,
  input  [31:0] Bank_2,
  input  [31:0] Bank_3,
  input  [3:0] ALU_Ope,
  input  [2:0] Branch_Ope,
  input  R___W,
  input  Inmediate_Operation,
  input  Logical_Inmediate,
  input  Hi_Lo_Ope,
  input  mfhi_mflo,
  input  RAM_Ope,
  input  lw,
  input  Stack_Ope,
  input  pop,
  input  En_SP,
  input  Load_PC,
  input  Load_Instruction,
  input  CLK,
  input  Reset,
  input  Hight_Op,
  input  Unsigned,
  output Zero_Div,
  output [5:0] Op_Code,
  output [5:0] Func_code,
  output [15:0] Address,
  output [1:0] Offset,
  output [3:0] Mask_prime,
  output [31:0] To_Ram
);

  wire and_1_out, C_Add, C_Rest, or_1_out, Rs_____Rt, Rs_____Rt_t, Rs_____Rt_t_t;
  wire [4:0] multiplexer_3_out, Rd, Rs, Rt, x;
  wire [15:0] Constant;
  wire [25:0] Destiny_Jump;
  wire [31:0] bit_extender_1_out, bit_extender_2_out, High, High_ALU, Instr, Low, Low_ALU, multiplexer_1_out,
       multiplexer_2_out, multiplexer_4_out, multiplexer_6_out, multiplexer_7_out, multiplexer_8_out, PC,
       PC_N, Register_Data, Rs_t, Rt_t, SP;

  and and_1 (and_1_out, R___W, ~Hight_Op);  // AND_Gate
  Multiplexer #(.width(32), .disabled(0), .enable("false")) multiplexer_1 (
    .in0(Low), .in1(High), .out(multiplexer_1_out), .sel(mfhi_mflo));
  ID_Program_Counter program_counter_1 (.PC(PC), .ENABLE(Load_PC), .CLCK(CLK), .RESET(Reset), .NEXT_PC(PC_N));
  // Branch_Control branch_control_1: pin names not known; wires that end beside it: Rs_t, PC_N, Constant, Destiny_Jump, Branch_Ope, Rs_____Rt_t, PC
  Multiplexer #(.width(32), .disabled(0), .enable("false")) multiplexer_2 (
    .in0(Low_ALU), .in1(multiplexer_1_out), .out(multiplexer_2_out), .sel(Hi_Lo_Ope));
  or or_1 (or_1_out, Inmediate_Operation, RAM_Ope);
  Multiplexer #(.width(5), .disabled(0), .enable("false")) multiplexer_3 (
    .in0(Rd), .in1(Rt), .out(multiplexer_3_out), .sel(or_1_out));
  Multiplexer #(.width(32), .disabled(0), .enable("false")) multiplexer_4 (
    .in0(multiplexer_2_out), .in1(Instr), .out(multiplexer_4_out), .sel(lw));
  ID_NEXT_ADRESS next_adress_1 (
    .PC(PC_N), .CONSTANT(Constant), .CHOSEN_R(Rs_t), .R31(SP), .STACK(Stack_Ope), .RAM(RAM_Ope),
    .ADRESS(Address), .OFFSET(Offset), .MASK(Mask_prime));
  Instruction_Decoder instruction_decoder_1 (
    .Input(Instr), .Load(Load_Instruction), .CLCK(CLK), .RESET(Reset), .OP_CODE(Op_Code),
    .JUMP(Destiny_Jump), .CONSTANT(Constant), .FUNC_CODE(Func_code), .RS(Rs), .RT(Rt), .RD(Rd), .X(x));
  Register_File register_file_1 (
    .CLCK(CLK), .Dato_de_Entrada(Register_Data), .RESET(Reset), .En_SP(En_SP), .pop(pop), .SA(Rs), .SB(Rt),
    .Enable(and_1_out), .Register_Address(multiplexer_3_out), .High(High_ALU), .Low(Low_ALU),
    .H_L_Enable(Hight_Op), .Salida_High(High), .Salida_Low(Low), .Salida_B(Rt_t), .Salida_A(Rs_t), .SP(SP));
  Multiplexer #(.width(32), .disabled(0), .enable("false")) multiplexer_5 (
    .in0(multiplexer_4_out), .in1(SP), .out(Register_Data), .sel(pop));
  assign bit_extender_1_out = {{16{Constant[15]}}, Constant};  // Bit_Extender bit_extender_1
  assign bit_extender_2_out = {{16{1'b0}}, Constant};  // Bit_Extender bit_extender_2
  Multiplexer #(.width(32), .disabled(0), .enable("false")) multiplexer_6 (
    .in0(bit_extender_1_out), .in1(bit_extender_2_out), .out(multiplexer_6_out), .sel(Logical_Inmediate));
  Little_Endian_Inmput little_endian_inmput_1 (.in_1(multiplexer_7_out), .out_2(Instr));
  Multiplexer #(.select(2), .width(32), .disabled(0), .enable("false")) multiplexer_7 (
    .in0(Bank_0), .in1(Bank_1), .in2(Bank_2), .in3(Bank_3), .out(multiplexer_7_out), .sel(Offset));
  Multiplexer #(.width(32), .disabled(0), .enable("false")) multiplexer_8 (
    .in0(Rt_t), .in1(multiplexer_6_out), .out(multiplexer_8_out), .sel(Inmediate_Operation));
  ALU alu_1 (
    .Rs(Rs_t), .Rt(multiplexer_8_out), .Select_Op(ALU_Ope), .Hight_Op(Hight_Op), .Unsigned(Unsigned),
    .Shoosed(Low_ALU), .Hight(High_ALU), .Great(Rs_____Rt_t_t), .Equal(Rs_____Rt_t), .Less(Rs_____Rt),
    .C_Add(C_Add), .C_Rest(C_Rest), .Div_x_0(Zero_Div));
  Little_Endian_Inmput little_endian_inmput_2 (.in_1(Rt_t), .out_2(To_Ram));

  // Other names for the same wires on the sheet: Inme = Inmediate_Operation; Load_instr = Load_Instruction;
  //   Logical_Inme = Logical_Inmediate; Mask[3:0] = Mask_prime; mfhi = mfhi_mflo; OpHight = Hight_Op; RST = Reset
endmodule

module Program_Counter (
  input  [31:0] PC,
  input  ENABLE,
  input  CLCK,
  input  RESET,
  output [31:0] NEXT_PC
);

  Register #(.width(32)) LOADING_PC (.D(PC), .en(ENABLE), .Q(NEXT_PC), .clk(CLCK), .clr(RESET));
endmodule

module NEXT_ADRESS (
  input  [31:0] PC,
  input  [15:0] CONSTANT,
  input  [31:0] CHOSEN_R,
  input  [31:0] R31,
  input  STACK,
  input  RAM,
  output [15:0] ADRESS,
  output [1:0] OFFSET,
  output [3:0] MASK
);

  wire [31:0] bit_extender_1_out, CR___CNST, multiplexer_1_out;

  assign bit_extender_1_out = {{16{CONSTANT[15]}}, CONSTANT};  // Bit_Extender bit_extender_1
  Adder #(.width(32)) adder_1 (.a(CHOSEN_R), .b(bit_extender_1_out), .out(CR___CNST));  // open: cin, cout
  Multiplexer #(.select(2), .width(32), .enable("false")) multiplexer_1 (
    .in0(PC), .in1(R31), .in2(CR___CNST),
    .out({multiplexer_1_out[31:20], ADRESS, OFFSET, multiplexer_1_out[1:0]}), .sel({RAM, STACK}));  // open: in3
  Demultiplexer #(.select(2), .enable("false")) demultiplexer_1 (
    .out0(MASK[0]), .out1(MASK[1]), .out2(MASK[2]), .out3(MASK[3]), .in(1'b1), .sel(OFFSET));

  // Other names for the same wires on the sheet: STACK_O = STACK; RAM_O = RAM; CNST[15:0] = CONSTANT
endmodule

module Instruction_Decoder (
  input  [31:0] Input,
  input  Load,
  input  CLCK,
  input  RESET,
  output [5:0] OP_CODE,
  output [25:0] JUMP,
  output [15:0] CONSTANT,
  output [5:0] FUNC_CODE,
  output [4:0] RS,
  output [4:0] RT,
  output [4:0] RD,
  output [4:0] X
);

  Register #(.width(32)) Instruction (
    .D(Input), .en(Load), .Q({OP_CODE, JUMP[25:16], CONSTANT}), .clk(CLCK), .clr(RESET));

  assign FUNC_CODE = CONSTANT[5:0];
  assign JUMP[15:0] = CONSTANT;
  assign RD = CONSTANT[15:11];
  assign RS = JUMP[25:21];
  assign RT = JUMP[20:16];
  assign X = CONSTANT[10:6];

  // Other names for the same wires on the sheet: CLOCK = CLCK;
  //   Final_Instruction[31:0] = {OP_CODE, JUMP[25:16], CONSTANT}; Instruction[31:0] = Input

  // Notes on the sheet:
  //   INPUT
  //   LOADING
  //   SEPARATION
  //   OUTPUT
endmodule

module ALU (
  input  [31:0] Rs,
  input  [31:0] Rt,
  input  [3:0] Select_Op,
  input  Hight_Op,
  input  Unsigned,
  output [31:0] Shoosed,
  output [31:0] Hight,
  output Great,
  output Equal,
  output Less,
  output C_Add,
  output C_Rest,
  output Div_x_0
);

  wire LessU, OpHight;
  wire [31:0] ADD, AND, DIV, Div_t, Divu, Mult, multiplexer_3_out, multiplexer_4_out, Mulu, NOR, OR, R_Div,
       R_Divu, R_Mult, R_Mulu, Slt, Sltu, SUB, XOR;

  assign AND = Rs & Rt;  // AND_Gate and_1, 32 bits wide
  assign OR = Rs | Rt;  // OR_Gate or_1, 32 bits wide
  assign XOR = Rs ^ Rt;  // XOR_Gate xor_1, 32 bits wide
  assign NOR = ~(Rs | Rt);  // NOR_Gate nor_1, 32 bits wide
  Adder #(.width(32)) adder_1 (.a(Rs), .b(Rt), .out(ADD), .cin(1'b0), .cout(C_Add));
  Subtractor #(.width(32)) subtractor_1 (.a(Rs), .b(Rt), .out(SUB), .bin(1'b0), .bout(C_Rest));
  Divu divu_1 (.Rs(Rs), .Lo(Divu), .Hi(R_Divu), .Rt(Rt));
  Comparator #(.width(32)) comparator_1 (.a(Rs), .b(Rt), .gt(Great), .eq(Equal), .lt(Less));
  Multiplexer #(.width(32), .enable("false")) multiplexer_1 (.in0({32{1'b0}}), .in1(32'h1), .out(Slt), .sel(Less));
  Multiplier #(.width(32)) multiplier_1 (.a(Rs), .b(Rt), .out(Mult), .cin({32{1'b0}}), .cout(R_Mult));
  Divider #(.width(32)) divider_1 (.a(Rs), .b(Rt), .out(DIV), .upper({32{1'b0}}), .rem(R_Div));
  Mulu mulu_1 (.Rs(Rs), .Lo(Mulu), .Hi(R_Mulu), .Rt(Rt));
  Comparator #(.width(32), .mode("unsigned")) comparator_2 (.a(Rs), .b(Rt), .lt(LessU));  // open: gt, eq
  Multiplexer #(.width(32), .enable("false")) multiplexer_2 (.in0({32{1'b0}}), .in1(32'h1), .out(Sltu), .sel(LessU));
  Multiplexer #(.width(32), .enable("false")) multiplexer_3 (
    .in0(R_Mult), .in1(R_Mulu), .out(multiplexer_3_out), .sel(Unsigned));
  Multiplexer #(.width(32), .enable("false")) multiplexer_4 (
    .in0(R_Div), .in1(R_Divu), .out(multiplexer_4_out), .sel(Unsigned));
  Multiplexer #(.select(4), .width(32), .enable("false")) multiplexer_5 (
    .in0(ADD), .in1(SUB), .in2(Mult), .in3(Mulu), .in4(Divu), .in5(Div_t), .in6(AND), .in7(OR), .in8(NOR),
    .in9(XOR), .in10(Slt), .in11(Sltu), .out(Shoosed), .sel(Select_Op));  // open: in12, in13, in14, in15
  Multiplexer #(.width(32), .enable("false")) multiplexer_6 (
    .in0(multiplexer_3_out), .in1(multiplexer_4_out), .out(Hight), .sel(OpHight));
  Comparator #(.width(32), .mode("unsigned")) comparator_3 (.a(Rt), .b({32{1'b0}}), .eq(Div_x_0));  // open: gt, lt

  // Other names for the same wires on the sheet: A[31:0] = Rs; B[31:0] = Rt; D0 = Div_x_0; Hi_S[31:0] = Hight;
  //   OpHight_t = Hight_Op

  // Notes on the sheet:
  //   Entradas
  //   Logical Operations
  //   Comparers
  //   Aritmetic Operations
  //   General Shooser
  //   Hight Shooser
  //   Cero Div
  //   Exits
  //   Flags
endmodule

module MULU (
  input  [31:0] Rs,
  input  [31:0] Rt,
  output [31:0] Lo,
  output [31:0] Hi
);

  wire [31:0] adder_1_out, multiplexer_1_out, multiplexer_2_out, multiplier_1_cout;

  Multiplexer #(.width(32), .enable("false")) multiplexer_1 (
    .in0({32{1'b0}}), .in1(Rs), .out(multiplexer_1_out), .sel(Rt[31]));
  Multiplexer #(.width(32), .enable("false")) multiplexer_2 (
    .in0({32{1'b0}}), .in1(Rt), .out(multiplexer_2_out), .sel(Rs[31]));
  Adder #(.width(32)) adder_1 (
    .a(multiplexer_1_out), .b(multiplexer_2_out), .out(adder_1_out), .cin(1'b0));  // open: cout
  Multiplier #(.width(32)) multiplier_1 (.a(Rs), .b(Rt), .out(Lo), .cin({32{1'b0}}), .cout(multiplier_1_cout));
  Adder #(.width(32)) adder_2 (.a(multiplier_1_cout), .b(adder_1_out), .out(Hi), .cin(1'b0));  // open: cout

  // Other names for the same wires on the sheet: A[31:0] = Rs; B[31:0] = Rt
endmodule

module DIVU (
  input  [31:0] Rs,
  input  [31:0] Rt,
  output [31:0] Lo,
  output [31:0] Hi
);

  wire xor_1_out;
  wire [31:0] divider_1_out, multiplexer_1_out, multiplexer_2_out, negator_1_out, negator_2_out,
       negator_3_out;

  Negator #(.width(32)) negator_1 (.in(Rs), .out(negator_1_out));
  Negator #(.width(32)) negator_2 (.in(Rt), .out(negator_2_out));
  Multiplexer #(.width(32), .enable("false")) multiplexer_1 (
    .in0(Rs), .in1(negator_1_out), .out(multiplexer_1_out), .sel(Rs[31]));
  Multiplexer #(.width(32), .enable("false")) multiplexer_2 (
    .in0(Rt), .in1(negator_2_out), .out(multiplexer_2_out), .sel(Rt[31]));
  Divider #(.width(32)) divider_1 (
    .a(multiplexer_1_out), .b(multiplexer_2_out), .out(divider_1_out), .rem(Hi));  // open: upper
  xor xor_1 (xor_1_out, Rs[31], Rt[31]);
  Negator #(.width(32)) negator_3 (.in(divider_1_out), .out(negator_3_out));
  Multiplexer #(.width(32), .enable("false")) multiplexer_3 (
    .in0(divider_1_out), .in1(negator_3_out), .out(Lo), .sel(xor_1_out));
endmodule

module Control_Unit (
  input  [5:0] Op_code,
  input  [5:0] Func_code,
  input  [3:0] Read_Time,
  input  [3:0] Write_Time,
  input  [15:0] Start,
  input  Clk,
  input  Reset,
  output [3:0] ALU_Ope,
  output [2:0] Branch_Ope,
  output En_SP,
  output Inmediate_Ope,
  output Logical_Inmediate_Ope,
  output R___W,
  output Hi_Lo_Ope,
  output mfhi,
  output RAM_Ope,
  output lw,
  output Stack_Ope,
  output pop,
  output Chip_Select,
  output RW_RAM,
  output Load_PC,
  output Load_Instuction
);

  wire comparator_1_eq, comparator_2_eq, comparator_4_eq, comparator_5_eq, comparator_6_eq, comparator_7_eq,
       CS_0, CS_1, CS_2, CS_3, CS_4, d_ff_2_q, d_ff_3_q, demultiplexer_1_out0, demultiplexer_1_out1,
       demultiplexer_2_out0, demultiplexer_3_out0, demultiplexer_3_out4, demultiplexer_3_out6,
       demultiplexer_4_out0, demultiplexer_4_out1, demultiplexer_5_out0, demultiplexer_5_out1,
       demultiplexer_6_out0, demultiplexer_6_out1, demultiplexer_6_out2, demultiplexer_6_out3,
       demultiplexer_7_out0, demultiplexer_7_out1, demultiplexer_8_out0, demultiplexer_9_out0,
       demultiplexer_10_out0, halt, IDLE_q, kbd, lw_t, nor_1_out, or_3_out, or_5_out, or_6_out, or_7_out,
       or_8_out, pop_t, R___W_1, rnd, tty, Wait;
  wire [1:0] Sp_Ope;
  wire [2:0] CU_Ope;
  wire [3:0] counter_1_q, RT____WT;
  wire [5:0] Op_Code_t;
  wire [10:0] End;
  wire [20:0] Big_part_of_it;
  wire [31:0] Instruction;

  // Ope_Func_Decode ope_func_decode_1: pin names not known; wires that end beside it: Op_code, Func_code, CU_Ope, ALU_Ope, Branch_Ope, Sp_Ope, pop_t, lw_t, mfhi, Logical_Inmediate_Ope
  D_Flip_Flop IDLE (.clk(Clk), .D(demultiplexer_1_out0), .Q(IDLE_q), .preset(Reset));  // open: Qn, en, reset
  Demultiplexer #(.disabled(0), .enable("false")) demultiplexer_1 (
    .out0(demultiplexer_1_out0), .out1(demultiplexer_1_out1), .in(IDLE_q), .sel(Reset));
  or or_1 (Chip_Select, CS_0, CS_1, CS_2, CS_3);
  buf or_2 (RW_RAM, CS_1);  // OR_Gate
  or or_3 (or_3_out, demultiplexer_2_out0, demultiplexer_1_out1);
  or or_4 (RAM_Ope, CS_1, CS_2, lw);
  D_Flip_Flop d_ff_1 (.clk(Clk), .D(or_3_out), .Q(CS_0), .reset(Reset));  // open: Qn, preset, en
  Demultiplexer #(.enable("false")) demultiplexer_2 (
    .out0(demultiplexer_2_out0), .out1(Load_Instuction), .in(CS_0), .sel(Wait));
  Multiplexer #(.width(4), .enable("false")) multiplexer_1 (
    .in0(Read_Time), .in1(Write_Time), .out(RT____WT), .sel(RW_RAM));
  D_Flip_Flop d_ff_2 (.clk(Clk), .D(Load_Instuction), .Q(d_ff_2_q), .reset(Reset));  // open: Qn, preset, en
  Demultiplexer #(.select(3), .disabled(0), .enable("false")) demultiplexer_3 (
    .out0(demultiplexer_3_out0), .out1(R___W_1), .out2(Inmediate_Ope), .out3(Hi_Lo_Ope),
    .out4(demultiplexer_3_out4), .out5(Stack_Ope), .out6(demultiplexer_3_out6), .in(d_ff_2_q), .sel(CU_Ope));  // open: out7
  D_Flip_Flop d_ff_3 (.clk(Clk), .D(Chip_Select), .Q(d_ff_3_q), .reset(Reset));  // open: Qn, preset, en
  Counter #(.width(4), .max('hf)) counter_1 (
    .load(Chip_Select), .D(RT____WT), .count(d_ff_3_q), .Q(counter_1_q), .clk(Clk));  // open: carry, clr
  nor nor_1 (nor_1_out, counter_1_q[0], counter_1_q[1], counter_1_q[2], counter_1_q[3]);
  Demultiplexer #(.disabled(0), .enable("false")) demultiplexer_4 (
    .out0(demultiplexer_4_out0), .out1(demultiplexer_4_out1), .in(demultiplexer_3_out4), .sel(lw_t));
  and and_1 (Wait, nor_1_out, d_ff_3_q);
  Demultiplexer #(.disabled(0), .enable("false")) demultiplexer_5 (
    .out0(demultiplexer_5_out0), .out1(demultiplexer_5_out1), .in(Stack_Ope), .sel(pop_t));
  Demultiplexer #(.select(2), .disabled(0), .enable("false")) demultiplexer_6 (
    .out0(demultiplexer_6_out0), .out1(demultiplexer_6_out1), .out2(demultiplexer_6_out2),
    .out3(demultiplexer_6_out3), .in(demultiplexer_3_out6), .sel(Sp_Ope));
  or or_5 (or_5_out, demultiplexer_7_out0, demultiplexer_4_out0);
  D_Flip_Flop d_ff_4 (.clk(Clk), .D(or_5_out), .Q(CS_1), .reset(Reset));  // open: Qn, preset, en
  or or_6 (or_6_out, demultiplexer_8_out0, demultiplexer_4_out1);
  or or_7 (or_7_out, demultiplexer_9_out0, demultiplexer_5_out0);
  or or_8 (or_8_out, demultiplexer_10_out0, demultiplexer_5_out1);
  Comparator #(.width(16)) comparator_1 (.a(16'hfc00), .b(Start), .eq(comparator_1_eq));  // open: gt, lt
  Comparator #(.width(11)) comparator_2 (.a(11'h2), .b(End), .eq(comparator_2_eq));  // open: gt, lt
  D_Flip_Flop d_ff_5 (.clk(Clk), .D(or_6_out), .Q(CS_2), .reset(Reset));  // open: Qn, preset, en
  D_Flip_Flop d_ff_6 (.clk(Clk), .D(or_7_out), .Q(CS_4), .reset(Reset));  // open: Qn, preset, en
  D_Flip_Flop d_ff_7 (.clk(Clk), .D(or_8_out), .Q(CS_3), .reset(Reset));  // open: Qn, preset, en
  Comparator #(.width(32)) comparator_3 (.a(Instruction), .b(32'h3f0000fc), .eq(halt));  // open: gt, lt
  and and_2 (rnd, comparator_1_eq, comparator_2_eq);
  Demultiplexer #(.enable("false")) demultiplexer_7 (
    .out0(demultiplexer_7_out0), .out1(demultiplexer_7_out1), .in(CS_1), .sel(Wait));
  Demultiplexer #(.enable("false")) demultiplexer_8 (.out0(demultiplexer_8_out0), .out1(lw), .in(CS_2), .sel(Wait));
  Demultiplexer #(.enable("false")) demultiplexer_9 (.out0(demultiplexer_9_out0), .in(CS_4), .sel(Wait));  // open: out1
  Demultiplexer #(.enable("false")) demultiplexer_10 (
    .out0(demultiplexer_10_out0), .out1(En_SP), .in(CS_3), .sel(Wait));
  Comparator #(.width(16)) comparator_4 (.a(16'hfc00), .b(Start), .eq(comparator_4_eq));  // open: gt, lt
  and and_3 (kbd, comparator_4_eq, comparator_5_eq);
  Comparator #(.width(11)) comparator_5 (.a(11'h4), .b(End), .eq(comparator_5_eq));  // open: gt, lt
  Comparator #(.width(6)) comparator_6 (.a({6{1'b1}}), .b(Op_Code_t), .eq(comparator_6_eq));  // open: gt, lt
  Comparator #(.width(21)) comparator_7 (.a(21'h1), .b(Big_part_of_it), .eq(comparator_7_eq));  // open: gt, lt
  and and_4 (tty, comparator_6_eq, comparator_7_eq);

  assign pop = En_SP;

  // Other names for the same wires on the sheet: CS = Chip_Select; Load_Inst = Load_Instuction;
  //   Logical_Inme_Ope = Logical_Inmediate_Ope; Inmedaite = Inmediate_Ope; R___W_2 = Inmediate_Ope;
  //   R___W_3 = Hi_Lo_Ope; R_W_RAM_1 = CS_1; RAM_Ope_1 = CS_1; RAM_Ope_2 = CS_2; RAM_Ope_4 = CS_3; R_W_RAM_2 = CS_4;
  //   RAM_Ope_5 = CS_4; RT[3:0] = Read_Time; RAM_Ope_3 = lw; S_lw = lw; R___W_4 = En_SP; S_pop = En_SP;
  //   WT[3:0] = Write_Time

  // Notes on the sheet:
  //   Input
  //   Ope-Func Decode
  //   Output
  //   Branch Operation
  //   ALU Operation
  //   Inmediate Operation
  //   Stack Operation
  //   Special Operation
  //   Wait for RT or WT
  //   Register Operation
  //   RAM Operation
  //   Store word
  //   Load word
  //   Push
  //   Pop
  //   Halt
  //   RANDOM
  //   SET KEY
  //   TTY
endmodule

module Op_Func_Decode (
  input  [5:0] Op_code,
  input  [5:0] Func_code,
  output [2:0] CU_Operation,
  output [3:0] ALU_Operation,
  output [2:0] Branch_Operation,
  output [1:0] Special_Ope,
  output pop,
  output mfhi,
  output lw,
  output Logical_Inme_Ope
);

  wire add, addi, AL_ope, \and , and_16_out, and_17_out, and_18_out, and_24_out, and_25_out, and_39_out,
       and_40_out, and_44_out, andi, beq, bgtz, blez, bltz, bne, Branch_Ope, div, divu, halt, Inme_Ope, j,
       jr, kbd, mflo, mult, mulu, nop, \nor , \or , or_9_out, or_10_out, or_11_out, or_12_out, or_13_out,
       or_14_out, or_15_out, ori, push, RAM_Ope, Registers_Ope, rnd, sliti, slitiu, slt, sltu, Special_Ope_t,
       Stack_Ope, sub, sw, tty, \xor , xori;

  and and_1 (add, ~Func_code[0], ~Func_code[1], ~Func_code[2], ~Func_code[3], ~Func_code[4], Func_code[5]);  // AND_Gate
  and and_2 (sub, ~Func_code[0], Func_code[1], ~Func_code[2], ~Func_code[3], ~Func_code[4], Func_code[5]);  // AND_Gate
  and and_3 (mult, ~Func_code[0], ~Func_code[1], ~Func_code[2], Func_code[3], Func_code[4], ~Func_code[5]);  // AND_Gate
  and and_4 (mulu, Func_code[0], ~Func_code[1], ~Func_code[2], Func_code[3], Func_code[4], ~Func_code[5]);  // AND_Gate
  and and_5 (div, ~Func_code[0], Func_code[1], ~Func_code[2], Func_code[3], Func_code[4], ~Func_code[5]);  // AND_Gate
  and and_6 (divu, Func_code[0], Func_code[1], ~Func_code[2], Func_code[3], Func_code[4], ~Func_code[5]);  // AND_Gate
  and and_7 (slt, ~Func_code[0], Func_code[1], ~Func_code[2], Func_code[3], ~Func_code[4], Func_code[5]);  // AND_Gate
  and and_8 (sltu, Func_code[0], Func_code[1], ~Func_code[2], Func_code[3], ~Func_code[4], Func_code[5]);  // AND_Gate
  and and_9 (\and , ~Func_code[0], ~Func_code[1], Func_code[2], ~Func_code[3], ~Func_code[4], Func_code[5]);  // AND_Gate
  and and_10 (\or , Func_code[0], ~Func_code[1], Func_code[2], ~Func_code[3], ~Func_code[4], Func_code[5]);  // AND_Gate
  and and_11 (\nor , Func_code[0], Func_code[1], Func_code[2], ~Func_code[3], ~Func_code[4], Func_code[5]);  // AND_Gate
  and and_12 (\xor , ~Func_code[0], ~Func_code[1], ~Func_code[2], Func_code[3], ~Func_code[4], Func_code[5]);  // AND_Gate
  and and_13 (jr, ~Func_code[0], ~Func_code[1], ~Func_code[2], Func_code[3], ~Func_code[4], ~Func_code[5]);  // AND_Gate
  and and_14 (mfhi, ~Func_code[0], ~Func_code[1], ~Func_code[2], ~Func_code[3], Func_code[4], ~Func_code[5]);  // AND_Gate
  and and_15 (mflo, ~Func_code[0], Func_code[1], ~Func_code[2], ~Func_code[3], Func_code[4], ~Func_code[5]);  // AND_Gate
  and and_16 (and_16_out, ~Func_code[0], ~Func_code[1], ~Func_code[2], ~Func_code[3], ~Func_code[4], ~Func_code[5]);  // AND_Gate
  and and_17 (and_17_out, ~Op_code[0], ~Op_code[1], ~Op_code[2], Op_code[3], Op_code[4], Op_code[5]);  // AND_Gate
  and and_18 (and_18_out, Func_code[0], ~Func_code[1], ~Func_code[2], ~Func_code[3], ~Func_code[4], ~Func_code[5]);  // AND_Gate
  and and_19 (pop, and_16_out, and_17_out);
  and and_20 (push, and_17_out, and_18_out);
  and and_21 (halt, Func_code[0], Func_code[1], Func_code[2], Func_code[3], Func_code[4], Func_code[5]);
  and and_22 (rnd, ~Func_code[0], Func_code[1], ~Func_code[2], ~Func_code[3], ~Func_code[4], ~Func_code[5]);  // AND_Gate
  and and_23 (kbd, ~Func_code[0], Func_code[1], ~Func_code[2], ~Func_code[3], ~Func_code[4], ~Func_code[5]);  // AND_Gate
  and and_24 (and_24_out, Func_code[0], ~Func_code[1], ~Func_code[2], ~Func_code[3], ~Func_code[4], ~Func_code[5]);  // AND_Gate
  and and_25 (and_25_out, Op_code[0], Op_code[1], Op_code[2], Op_code[3], Op_code[4], Op_code[5]);
  and and_26 (tty, and_24_out, and_25_out);
  and and_27 (addi, ~Op_code[0], ~Op_code[1], ~Op_code[2], Op_code[3], ~Op_code[4], ~Op_code[5]);  // AND_Gate
  and and_28 (sliti, ~Op_code[0], Op_code[1], ~Op_code[2], Op_code[3], ~Op_code[4], ~Op_code[5]);  // AND_Gate
  and and_29 (slitiu, Op_code[0], Op_code[1], ~Op_code[2], Op_code[3], ~Op_code[4], ~Op_code[5]);  // AND_Gate
  and and_30 (andi, ~Op_code[0], ~Op_code[1], Op_code[2], Op_code[3], ~Op_code[4], ~Op_code[5]);  // AND_Gate
  and and_31 (ori, Op_code[0], ~Op_code[1], Op_code[2], Op_code[3], ~Op_code[4], ~Op_code[5]);  // AND_Gate
  and and_32 (xori, ~Op_code[0], Op_code[1], Op_code[2], Op_code[3], ~Op_code[4], ~Op_code[5]);  // AND_Gate
  and and_33 (beq, ~Op_code[0], ~Op_code[1], Op_code[2], ~Op_code[3], ~Op_code[4], ~Op_code[5]);  // AND_Gate
  and and_34 (bne, Op_code[0], ~Op_code[1], Op_code[2], ~Op_code[3], ~Op_code[4], ~Op_code[5]);  // AND_Gate
  and and_35 (blez, ~Op_code[0], Op_code[1], Op_code[2], ~Op_code[3], ~Op_code[4], ~Op_code[5]);  // AND_Gate
  and and_36 (bgtz, Op_code[0], Op_code[1], Op_code[2], ~Op_code[3], ~Op_code[4], ~Op_code[5]);  // AND_Gate
  and and_37 (bltz, Op_code[0], ~Op_code[1], ~Op_code[2], ~Op_code[3], ~Op_code[4], ~Op_code[5]);  // AND_Gate
  and and_38 (j, ~Op_code[0], Op_code[1], ~Op_code[2], ~Op_code[3], ~Op_code[4], ~Op_code[5]);  // AND_Gate
  and and_39 (and_39_out, ~Op_code[0], ~Op_code[1], ~Op_code[2], ~Op_code[3], ~Op_code[4], ~Op_code[5]);  // AND_Gate
  and and_40 (and_40_out, ~Func_code[0], ~Func_code[1], ~Func_code[2], ~Func_code[3], ~Func_code[4], ~Func_code[5]);  // AND_Gate
  buf and_41 (nop, and_39_out);  // AND_Gate
  and and_42 (lw, Op_code[0], Op_code[1], ~Op_code[2], ~Op_code[3], ~Op_code[4], Op_code[5]);  // AND_Gate
  and and_43 (sw, Op_code[0], Op_code[1], ~Op_code[2], Op_code[3], ~Op_code[4], Op_code[5]);  // AND_Gate
  or or_1 (Stack_Ope, pop, push);
  or or_2 (RAM_Ope, lw, sw);
  or or_3 (Registers_Ope, mfhi, mflo);
  or or_4 (AL_ope, add, sub, mult, mulu, div, divu, slt, sltu, \and , \or , \nor , \xor );
  or or_5 (Branch_Ope, nop, beq, bne, blez, bgtz, bltz, j, jr);
  or or_6 (Inme_Ope, addi, sliti, slitiu, andi, ori, xori);
  or or_7 (Logical_Inme_Ope, andi, ori, xori);
  or or_8 (Special_Ope_t, halt, rnd, kbd, tty);
  or or_9 (or_9_out, add, addi);
  or or_10 (or_10_out, \and , andi);
  or or_11 (or_11_out, \or , ori);
  or or_12 (or_12_out, \xor , xori);
  or or_13 (or_13_out, slt, sliti);
  or or_14 (or_14_out, sltu, slitiu);
  and and_44 (and_44_out, ~AL_ope, ~Inme_Ope);  // AND_Gate
  or or_15 (or_15_out, halt, 1'b1);
  Priority_Encoder #(.disabled(0)) priority_encoder_1 (
    .in0(Branch_Ope), .in1(AL_ope), .in2(Inme_Ope), .in3(Registers_Ope), .in4(RAM_Ope), .in5(Stack_Ope),
    .in6(Special_Ope_t), .out(CU_Operation), .en_in(1'b1));  // open: in7, gs, en_out
  Priority_Encoder #(.select(4), .disabled(0)) priority_encoder_2 (
    .in0(or_9_out), .in1(sub), .in2(mult), .in3(mulu), .in4(div), .in5(divu), .in6(or_10_out),
    .in7(or_11_out), .in8(\nor ), .in9(or_12_out), .in10(or_13_out), .in11(or_14_out), .in15(and_44_out),
    .out(ALU_Operation), .en_in(1'b1));  // open: in12, in13, in14, gs, en_out
  Priority_Encoder #(.disabled(0)) priority_encoder_3 (
    .in0(1'b1), .in1(beq), .in2(bne), .in3(blez), .in4(bgtz), .in5(bltz), .in6(j), .in7(jr),
    .out(Branch_Operation), .en_in(1'b1));  // open: gs, en_out
  Priority_Encoder #(.select(2), .disabled(0)) priority_encoder_4 (
    .in0(or_15_out), .in1(tty), .in2(rnd), .in3(kbd), .out(Special_Ope), .en_in(1'b1));  // open: gs, en_out

  // Notes on the sheet:
  //   Input
  //   ALU
  //   Register
  //   Func-code Decode
  //   Stack
  //   Special
  //   ALU
  //   Op-code Decode
  //   BRANCH
  //   RAM
  //   Operation Clasifier
  //   Output
  //   Control Unit Operation Encoder
  //   ALU Operation Encoder
  //   Branch Operation Encoder
  //   Special Operation Encoder
  //   Others  Operations
endmodule
