// Logisim project ID.circ as structural Verilog: 4 circuits, main circuit main
module main (
  input  [31:0] Input,
  output [5:0] OP_CODE,
  output [25:0] JUMP,
  output [15:0] CONSTANT,
  output [5:0] FUNC_CODE,
  output [4:0] RS,
  output [4:0] RT,
  output [4:0] RD,
  output [4:0] X
);

  wire CLOCK, Load, Reset;

  Register #(.width(32)) Instruction (
    .D(Input), .en(Load), .Q({OP_CODE, JUMP[25:16], CONSTANT}), .clk(CLOCK), .clr(Reset));

  assign FUNC_CODE = CONSTANT[5:0];
  assign JUMP[15:0] = CONSTANT;
  assign RD = CONSTANT[15:11];
  assign RS = JUMP[25:21];
  assign RT = JUMP[20:16];
  assign X = CONSTANT[10:6];

  // Other names for the same wires on the sheet: Final_Instruction[31:0] = {OP_CODE, JUMP[25:16], CONSTANT};
  //   Instruction[31:0] = Input

  // Notes on the sheet:
  //   INPUT
  //   LOADING
  //   SEPARATION
  //   OUTPUT
endmodule

module Program_Counter (
  input  [31:0] PC,
  input  ENABLE,
  input  CLCK,
  input  RESET,
  output [31:0] NEXT_PC
);

  Register #(.width(32)) LOADING_PC (.D(PC), .en(ENABLE), .Q(NEXT_PC), .clk(CLCK), .clr(RESET));
endmodule

module NEXT_ADRESS (
  input  [31:0] PC,
  input  [15:0] CONSTANT,
  input  [31:0] CHOSEN_R,
  input  [31:0] R31,
  input  STACK,
  input  RAM,
  output [15:0] ADRESS,
  output [1:0] OFFSET,
  output [3:0] MASK
);

  wire [31:0] bit_extender_1_out, CR___CNST, multiplexer_1_out;

  assign bit_extender_1_out = {{16{CONSTANT[15]}}, CONSTANT};  // Bit_Extender bit_extender_1
  Adder #(.width(32)) adder_1 (.a(CHOSEN_R), .b(bit_extender_1_out), .out(CR___CNST));  // open: cin, cout
  Multiplexer #(.select(2), .width(32), .enable("false")) multiplexer_1 (
    .in0(PC), .in1(R31), .in2(CR___CNST),
    .out({multiplexer_1_out[31:20], ADRESS, OFFSET, multiplexer_1_out[1:0]}), .sel({RAM, STACK}));  // open: in3
  Demultiplexer #(.select(2), .enable("false")) demultiplexer_1 (
    .out0(MASK[0]), .out1(MASK[1]), .out2(MASK[2]), .out3(MASK[3]), .in(1'b1), .sel(OFFSET));

  // Other names for the same wires on the sheet: STACK_O = STACK; RAM_O = RAM; CNST[15:0] = CONSTANT
endmodule

module Codefied (
  input  [5:0] OP_CODE,
  input  [5:0] FUNC_CODE,
  output [2:0] CU_Operation,
  output [3:0] ALU_Operation,
  output [2:0] Branch_Operation,
  output [1:0] Special_Ope,
  output pop,
  output mfhi,
  output lw,
  output Logical_Inme_Ope
);

  wire ADD, ADDI, AL_O, AND, and_16_out, and_17_out, and_18_out, and_24_out, and_25_out, and_42_out, ANDI,
       BEQ, BGTZ, BLEZ, BLTZ, BNE, Branch_O, DIV, DIVU, HALT, Inme_O, J, JR, KBD, MFLO, MULT, MULU, NOP, NOR,
       OR, or_9_out, or_10_out, or_11_out, or_12_out, or_13_out, or_14_out, or_15_out, ORI, PUSH, RAM_O,
       Registers_O, RND, SLITI, SLITIU, SLT, SLTU, Special_O, Stack_O, SUB, SW, TTY, XOR, XORI;

  and and_1 (ADD, ~FUNC_CODE[0], ~FUNC_CODE[1], ~FUNC_CODE[2], ~FUNC_CODE[3], ~FUNC_CODE[4], FUNC_CODE[5]);  // AND_Gate
  and and_2 (SUB, ~FUNC_CODE[0], FUNC_CODE[1], ~FUNC_CODE[2], ~FUNC_CODE[3], ~FUNC_CODE[4], FUNC_CODE[5]);  // AND_Gate
  and and_3 (MULT, ~FUNC_CODE[0], ~FUNC_CODE[1], ~FUNC_CODE[2], FUNC_CODE[3], FUNC_CODE[4], ~FUNC_CODE[5]);  // AND_Gate
  and and_4 (MULU, FUNC_CODE[0], ~FUNC_CODE[1], ~FUNC_CODE[2], FUNC_CODE[3], FUNC_CODE[4], ~FUNC_CODE[5]);  // AND_Gate
  and and_5 (DIV, ~FUNC_CODE[0], FUNC_CODE[1], ~FUNC_CODE[2], FUNC_CODE[3], FUNC_CODE[4], ~FUNC_CODE[5]);  // AND_Gate
  and and_6 (DIVU, FUNC_CODE[0], FUNC_CODE[1], ~FUNC_CODE[2], FUNC_CODE[3], FUNC_CODE[4], ~FUNC_CODE[5]);  // AND_Gate
  and and_7 (SLT, ~FUNC_CODE[0], FUNC_CODE[1], ~FUNC_CODE[2], FUNC_CODE[3], ~FUNC_CODE[4], FUNC_CODE[5]);  // AND_Gate
  and and_8 (SLTU, FUNC_CODE[0], FUNC_CODE[1], ~FUNC_CODE[2], FUNC_CODE[3], ~FUNC_CODE[4], FUNC_CODE[5]);  // AND_Gate
  and and_9 (AND, ~FUNC_CODE[0], ~FUNC_CODE[1], FUNC_CODE[2], ~FUNC_CODE[3], ~FUNC_CODE[4], FUNC_CODE[5]);  // AND_Gate
  and and_10 (OR, FUNC_CODE[0], ~FUNC_CODE[1], FUNC_CODE[2], ~FUNC_CODE[3], ~FUNC_CODE[4], FUNC_CODE[5]);  // AND_Gate
  and and_11 (NOR, FUNC_CODE[0], FUNC_CODE[1], FUNC_CODE[2], ~FUNC_CODE[3], ~FUNC_CODE[4], FUNC_CODE[5]);  // AND_Gate
  and and_12 (XOR, ~FUNC_CODE[0], ~FUNC_CODE[1], ~FUNC_CODE[2], FUNC_CODE[3], ~FUNC_CODE[4], FUNC_CODE[5]);  // AND_Gate
  and and_13 (JR, ~FUNC_CODE[0], ~FUNC_CODE[1], ~FUNC_CODE[2], FUNC_CODE[3], ~FUNC_CODE[4], ~FUNC_CODE[5]);  // AND_Gate
  and and_14 (mfhi, ~FUNC_CODE[0], ~FUNC_CODE[1], ~FUNC_CODE[2], ~FUNC_CODE[3], FUNC_CODE[4], ~FUNC_CODE[5]);  // AND_Gate
  and and_15 (MFLO, ~FUNC_CODE[0], FUNC_CODE[1], ~FUNC_CODE[2], ~FUNC_CODE[3], FUNC_CODE[4], ~FUNC_CODE[5]);  // AND_Gate
  and and_16 (and_16_out, ~FUNC_CODE[0], ~FUNC_CODE[1], ~FUNC_CODE[2], ~FUNC_CODE[3], ~FUNC_CODE[4], ~FUNC_CODE[5]);  // AND_Gate
  and and_17 (and_17_out, ~FUNC_CODE[0], ~FUNC_CODE[1], ~FUNC_CODE[2], FUNC_CODE[3], FUNC_CODE[4], FUNC_CODE[5]);  // AND_Gate
  and and_18 (and_18_out, FUNC_CODE[0], ~FUNC_CODE[1], ~FUNC_CODE[2], ~FUNC_CODE[3], ~FUNC_CODE[4], ~FUNC_CODE[5]);  // AND_Gate
  and and_19 (pop, and_16_out, and_17_out);
  and and_20 (PUSH, and_17_out, and_18_out);
  and and_21 (HALT, FUNC_CODE[0], FUNC_CODE[1], FUNC_CODE[2], FUNC_CODE[3], FUNC_CODE[4], FUNC_CODE[5]);
  and and_22 (RND, ~FUNC_CODE[0], FUNC_CODE[1], ~FUNC_CODE[2], ~FUNC_CODE[3], ~FUNC_CODE[4], ~FUNC_CODE[5]);  // AND_Gate
  and and_23 (KBD, ~FUNC_CODE[0], FUNC_CODE[1], ~FUNC_CODE[2], ~FUNC_CODE[3], ~FUNC_CODE[4], ~FUNC_CODE[5]);  // AND_Gate
  and and_24 (and_24_out, FUNC_CODE[0], ~FUNC_CODE[1], ~FUNC_CODE[2], ~FUNC_CODE[3], ~FUNC_CODE[4], ~FUNC_CODE[5]);  // AND_Gate
  and and_25 (and_25_out, FUNC_CODE[0], FUNC_CODE[1], FUNC_CODE[2], FUNC_CODE[3], FUNC_CODE[4], FUNC_CODE[5]);
  and and_26 (TTY, and_24_out, and_25_out);
  and and_27 (ADDI, ~OP_CODE[0], ~OP_CODE[1], ~OP_CODE[2], OP_CODE[3], ~OP_CODE[4], ~OP_CODE[5]);  // AND_Gate
  and and_28 (SLITI, ~OP_CODE[0], OP_CODE[1], ~OP_CODE[2], OP_CODE[3], ~OP_CODE[4], ~OP_CODE[5]);  // AND_Gate
  and and_29 (SLITIU, OP_CODE[0], OP_CODE[1], ~OP_CODE[2], OP_CODE[3], ~OP_CODE[4], ~OP_CODE[5]);  // AND_Gate
  and and_30 (ANDI, ~OP_CODE[0], ~OP_CODE[1], OP_CODE[2], OP_CODE[3], ~OP_CODE[4], ~OP_CODE[5]);  // AND_Gate
  and and_31 (ORI, OP_CODE[0], ~OP_CODE[1], OP_CODE[2], OP_CODE[3], ~OP_CODE[4], ~OP_CODE[5]);  // AND_Gate
  and and_32 (XORI, ~OP_CODE[0], OP_CODE[1], OP_CODE[2], OP_CODE[3], ~OP_CODE[4], ~OP_CODE[5]);  // AND_Gate
  and and_33 (BEQ, ~OP_CODE[0], ~OP_CODE[1], OP_CODE[2], ~OP_CODE[3], ~OP_CODE[4], ~OP_CODE[5]);  // AND_Gate
  and and_34 (BNE, OP_CODE[0], ~OP_CODE[1], OP_CODE[2], ~OP_CODE[3], ~OP_CODE[4], ~OP_CODE[5]);  // AND_Gate
  and and_35 (BLEZ, ~OP_CODE[0], OP_CODE[1], OP_CODE[2], ~OP_CODE[3], ~OP_CODE[4], ~OP_CODE[5]);  // AND_Gate
  and and_36 (BGTZ, OP_CODE[0], OP_CODE[1], OP_CODE[2], ~OP_CODE[3], ~OP_CODE[4], ~OP_CODE[5]);  // AND_Gate
  and and_37 (BLTZ, OP_CODE[0], ~OP_CODE[1], ~OP_CODE[2], ~OP_CODE[3], ~OP_CODE[4], ~OP_CODE[5]);  // AND_Gate
  and and_38 (J, ~OP_CODE[0], OP_CODE[1], ~OP_CODE[2], ~OP_CODE[3], ~OP_CODE[4], ~OP_CODE[5]);  // AND_Gate
  and and_39 (NOP, ~OP_CODE[0], ~OP_CODE[1], ~OP_CODE[2], ~OP_CODE[3], ~OP_CODE[4], ~OP_CODE[5]);  // AND_Gate
  and and_40 (lw, OP_CODE[0], OP_CODE[1], ~OP_CODE[2], ~OP_CODE[3], ~OP_CODE[4], OP_CODE[5]);  // AND_Gate
  and and_41 (SW, OP_CODE[0], OP_CODE[1], ~OP_CODE[2], OP_CODE[3], ~OP_CODE[4], OP_CODE[5]);  // AND_Gate
  or or_1 (Stack_O, pop, PUSH);
  or or_2 (RAM_O, lw, SW);
  or or_3 (Registers_O, mfhi, MFLO);
  or or_4 (AL_O, ADD, SUB, MULT, MULU, DIV, DIVU, SLT, SLTU, AND, OR, NOR, XOR);
  or or_5 (Branch_O, NOP, BEQ, BNE, BLEZ, BGTZ, BLTZ, J, JR);
  or or_6 (Inme_O, ADDI, SLITI, SLITIU, ANDI, ORI, XORI);
  or or_7 (Logical_Inme_Ope, ANDI, ORI, XORI);
  or or_8 (Special_O, HALT, RND, KBD, TTY);
  or or_9 (or_9_out, ADD, ADDI);
  or or_10 (or_10_out, AND, ANDI);
  or or_11 (or_11_out, OR, ORI);
  or or_12 (or_12_out, XOR, XORI);
  or or_13 (or_13_out, SLT, SLITI);
  or or_14 (or_14_out, SLTU, SLITIU);
  and and_42 (and_42_out, ~AL_O, ~Inme_O);  // AND_Gate
  or or_15 (or_15_out, HALT, 1'b1);
  Priority_Encoder #(.disabled(0)) priority_encoder_1 (
    .in0(Branch_O), .in1(AL_O), .in2(Inme_O), .in3(Registers_O), .in4(RAM_O), .in5(Stack_O), .in6(Special_O),
    .out(CU_Operation), .en_in(1'b1));  // open: in7, gs, en_out
  Priority_Encoder #(.select(4), .disabled(0)) priority_encoder_2 (
    .in0(or_9_out), .in1(SUB), .in2(MULT), .in3(MULU), .in4(DIV), .in5(DIVU), .in6(or_10_out),
    .in7(or_11_out), .in8(NOR), .in9(or_12_out), .in10(or_13_out), .in11(or_14_out), .in15(and_42_out),
    .out(ALU_Operation), .en_in(1'b1));  // open: in12, in13, in14, gs, en_out
  Priority_Encoder #(.disabled(0)) priority_encoder_3 (
    .in0(1'b1), .in1(BEQ), .in2(BNE), .in3(BLEZ), .in4(BGTZ), .in5(BLTZ), .in6(J), .in7(JR),
    .out(Branch_Operation), .en_in(1'b1));  // open: gs, en_out
  Priority_Encoder #(.select(2), .disabled(0)) priority_encoder_4 (
    .in0(or_15_out), .in1(TTY), .in2(RND), .in3(KBD), .out(Special_Ope), .en_in(1'b1));  // open: gs, en_out

  // Other names for the same wires on the sheet: Logical_Inme_O = Logical_Inme_Ope

  // Notes on the sheet:
  //   Input
  //   ALU
  //   Register
  //   Func-code Decode
  //   Stack
  //   Special
  //   ALU
  //   Op-code Decode
  //   BRANCH
  //   RAM
  //   Operation Clasifier
  //   Output
  //   Control Unit Operation Encoder
  //   ALU Operation Encoder
  //   Branch Operation Encoder
  //   Special Operation Encoder
  //   Others  Operations
endmodule
