// Logisim project Registros.circ as structural Verilog
module Registro_Paralelo_32_bits (
  input  in_1,
  input  in_2,
  input  in_3,
  input  in_4,
  input  in_5,
  input  in_6,
  input  in_7,
  input  in_8,
  input  in_9,
  input  in_10,
  input  in_11,
  input  in_12,
  input  in_13,
  input  in_14,
  input  in_15,
  input  in_16,
  input  in_17,
  input  in_18,
  input  in_19,
  input  in_20,
  input  in_21,
  input  in_22,
  input  in_23,
  input  in_24,
  input  in_25,
  input  in_26,
  input  in_27,
  input  in_28,
  input  in_29,
  input  in_30,
  input  in_31,
  input  in_32,
  output out_33,
  output out_34,
  output out_35,
  output out_36,
  output out_37,
  output out_38,
  output out_39,
  output out_40,
  output out_41,
  output out_42,
  output out_43,
  output out_44,
  output out_45,
  output out_46,
  output out_47,
  output out_48,
  output out_49,
  output out_50,
  output out_51,
  output out_52,
  output out_53,
  output out_54,
  output out_55,
  output out_56,
  output out_57,
  output out_58,
  output out_59,
  output out_60,
  output out_61,
  output out_62,
  output out_63,
  output out_64
);

  wire clock_1_out;

  Clock clock_1 (.out(clock_1_out));
  D_Flip_Flop d_ff_1 (.clk(clock_1_out), .D(in_1), .Q(out_33));  // open: Qn, preset, en, reset
  D_Flip_Flop d_ff_2 (.clk(clock_1_out), .D(in_11), .Q(out_43));  // open: Qn, preset, en, reset
  D_Flip_Flop d_ff_3 (.clk(clock_1_out), .D(in_21), .Q(out_53));  // open: Qn, preset, en, reset
  D_Flip_Flop d_ff_4 (.clk(clock_1_out), .D(in_2), .Q(out_34));  // open: Qn, preset, en, reset
  D_Flip_Flop d_ff_5 (.clk(clock_1_out), .D(in_12), .Q(out_44));  // open: Qn, preset, en, reset
  D_Flip_Flop d_ff_6 (.clk(clock_1_out), .D(in_22), .Q(out_54));  // open: Qn, preset, en, reset
  D_Flip_Flop d_ff_7 (.clk(clock_1_out), .D(in_3), .Q(out_35));  // open: Qn, preset, en, reset
  D_Flip_Flop d_ff_8 (.clk(clock_1_out), .D(in_13), .Q(out_45));  // open: Qn, preset, en, reset
  D_Flip_Flop d_ff_9 (.clk(clock_1_out), .D(in_23), .Q(out_55));  // open: Qn, preset, en, reset
  D_Flip_Flop d_ff_10 (.clk(clock_1_out), .D(in_4), .Q(out_36));  // open: Qn, preset, en, reset
  D_Flip_Flop d_ff_11 (.clk(clock_1_out), .D(in_14), .Q(out_46));  // open: Qn, preset, en, reset
  D_Flip_Flop d_ff_12 (.clk(clock_1_out), .D(in_24), .Q(out_56));  // open: Qn, preset, en, reset
  D_Flip_Flop d_ff_13 (.clk(clock_1_out), .D(in_5), .Q(out_37));  // open: Qn, preset, en, reset
  D_Flip_Flop d_ff_14 (.clk(clock_1_out), .D(in_15), .Q(out_47));  // open: Qn, preset, en, reset
  D_Flip_Flop d_ff_15 (.clk(clock_1_out), .D(in_25), .Q(out_57));  // open: Qn, preset, en, reset
  D_Flip_Flop d_ff_16 (.clk(clock_1_out), .D(in_31), .Q(out_64));  // open: Qn, preset, en, reset
  D_Flip_Flop d_ff_17 (.clk(clock_1_out), .D(in_6), .Q(out_38));  // open: Qn, preset, en, reset
  D_Flip_Flop d_ff_18 (.clk(clock_1_out), .D(in_16), .Q(out_48));  // open: Qn, preset, en, reset
  D_Flip_Flop d_ff_19 (.clk(clock_1_out), .D(in_26), .Q(out_58));  // open: Qn, preset, en, reset
  D_Flip_Flop d_ff_20 (.clk(clock_1_out), .D(in_32), .Q(out_63));  // open: Qn, preset, en, reset
  D_Flip_Flop d_ff_21 (.clk(clock_1_out), .D(in_7), .Q(out_39));  // open: Qn, preset, en, reset
  D_Flip_Flop d_ff_22 (.clk(clock_1_out), .D(in_17), .Q(out_49));  // open: Qn, preset, en, reset
  D_Flip_Flop d_ff_23 (.clk(clock_1_out), .D(in_27), .Q(out_59));  // open: Qn, preset, en, reset
  D_Flip_Flop d_ff_24 (.clk(clock_1_out), .D(in_8), .Q(out_40));  // open: Qn, preset, en, reset
  D_Flip_Flop d_ff_25 (.clk(clock_1_out), .D(in_18), .Q(out_50));  // open: Qn, preset, en, reset
  D_Flip_Flop d_ff_26 (.clk(clock_1_out), .D(in_28), .Q(out_60));  // open: Qn, preset, en, reset
  D_Flip_Flop d_ff_27 (.clk(clock_1_out), .D(in_9), .Q(out_41));  // open: Qn, preset, en, reset
  D_Flip_Flop d_ff_28 (.clk(clock_1_out), .D(in_19), .Q(out_51));  // open: Qn, preset, en, reset
  D_Flip_Flop d_ff_29 (.clk(clock_1_out), .D(in_29), .Q(out_61));  // open: Qn, preset, en, reset
  D_Flip_Flop d_ff_30 (.clk(clock_1_out), .D(in_10), .Q(out_42));  // open: Qn, preset, en, reset
  D_Flip_Flop d_ff_31 (.clk(clock_1_out), .D(in_20), .Q(out_52));  // open: Qn, preset, en, reset
  D_Flip_Flop d_ff_32 (.clk(clock_1_out), .D(in_30), .Q(out_62));  // open: Qn, preset, en, reset
endmodule

module Registro_Serie_32_bits (
  input  in_1,
  output out_2,
  output out_3,
  output out_4,
  output out_5,
  output out_6,
  output out_7,
  output out_8,
  output out_9,
  output out_10,
  output out_11,
  output out_12,
  output out_13,
  output out_14,
  output out_15,
  output out_16,
  output out_17,
  output out_18,
  output out_19,
  output out_20,
  output out_21,
  output out_22,
  output out_23,
  output out_24,
  output out_25,
  output out_26,
  output out_27,
  output out_28,
  output out_29,
  output out_30,
  output out_31,
  output out_32,
  output out_33
);

  wire clock_1_out;

  Clock clock_1 (.out(clock_1_out));
  D_Flip_Flop d_ff_1 (.clk(clock_1_out), .D(in_1), .Q(out_2));  // open: Qn, preset, en, reset
  D_Flip_Flop d_ff_2 (.clk(clock_1_out), .D(out_11), .Q(out_12));  // open: Qn, preset, en, reset
  D_Flip_Flop d_ff_3 (.clk(clock_1_out), .D(out_21), .Q(out_22));  // open: Qn, preset, en, reset
  D_Flip_Flop d_ff_4 (.clk(clock_1_out), .D(out_2), .Q(out_3));  // open: Qn, preset, en, reset
  D_Flip_Flop d_ff_5 (.clk(clock_1_out), .D(out_12), .Q(out_13));  // open: Qn, preset, en, reset
  D_Flip_Flop d_ff_6 (.clk(clock_1_out), .D(out_22), .Q(out_23));  // open: Qn, preset, en, reset
  D_Flip_Flop d_ff_7 (.clk(clock_1_out), .D(out_3), .Q(out_4));  // open: Qn, preset, en, reset
  D_Flip_Flop d_ff_8 (.clk(clock_1_out), .D(out_13), .Q(out_14));  // open: Qn, preset, en, reset
  D_Flip_Flop d_ff_9 (.clk(clock_1_out), .D(out_23), .Q(out_24));  // open: Qn, preset, en, reset
  D_Flip_Flop d_ff_10 (.clk(clock_1_out), .D(out_4), .Q(out_5));  // open: Qn, preset, en, reset
  D_Flip_Flop d_ff_11 (.clk(clock_1_out), .D(out_14), .Q(out_15));  // open: Qn, preset, en, reset
  D_Flip_Flop d_ff_12 (.clk(clock_1_out), .D(out_24), .Q(out_25));  // open: Qn, preset, en, reset
  D_Flip_Flop d_ff_13 (.clk(clock_1_out), .D(out_5), .Q(out_6));  // open: Qn, preset, en, reset
  D_Flip_Flop d_ff_14 (.clk(clock_1_out), .D(out_15), .Q(out_16));  // open: Qn, preset, en, reset
  D_Flip_Flop d_ff_15 (.clk(clock_1_out), .Q(out_26));  // open: D, Qn, preset, en, reset
  D_Flip_Flop d_ff_16 (.clk(clock_1_out), .D(out_31), .Q(out_33));  // open: Qn, preset, en, reset
  D_Flip_Flop d_ff_17 (.clk(clock_1_out), .D(out_6), .Q(out_7));  // open: Qn, preset, en, reset
  D_Flip_Flop d_ff_18 (.clk(clock_1_out), .D(out_16), .Q(out_17));  // open: Qn, preset, en, reset
  D_Flip_Flop d_ff_19 (.clk(clock_1_out), .D(out_26), .Q(out_27));  // open: Qn, preset, en, reset
  D_Flip_Flop d_ff_20 (.clk(clock_1_out), .D(out_33), .Q(out_32));  // open: Qn, preset, en, reset
  D_Flip_Flop d_ff_21 (.clk(clock_1_out), .D(out_7), .Q(out_8));  // open: Qn, preset, en, reset
  D_Flip_Flop d_ff_22 (.clk(clock_1_out), .D(out_17), .Q(out_18));  // open: Qn, preset, en, reset
  D_Flip_Flop d_ff_23 (.clk(clock_1_out), .D(out_27), .Q(out_28));  // open: Qn, preset, en, reset
  D_Flip_Flop d_ff_24 (.clk(clock_1_out), .D(out_8), .Q(out_9));  // open: Qn, preset, en, reset
  D_Flip_Flop d_ff_25 (.clk(clock_1_out), .D(out_18), .Q(out_19));  // open: Qn, preset, en, reset
  D_Flip_Flop d_ff_26 (.clk(clock_1_out), .D(out_28), .Q(out_29));  // open: Qn, preset, en, reset
  D_Flip_Flop d_ff_27 (.clk(clock_1_out), .D(out_9), .Q(out_10));  // open: Qn, preset, en, reset
  D_Flip_Flop d_ff_28 (.clk(clock_1_out), .D(out_19), .Q(out_20));  // open: Qn, preset, en, reset
  D_Flip_Flop d_ff_29 (.clk(clock_1_out), .D(out_29), .Q(out_30));  // open: Qn, preset, en, reset
  D_Flip_Flop d_ff_30 (.clk(clock_1_out), .D(out_10), .Q(out_11));  // open: Qn, preset, en, reset
  D_Flip_Flop d_ff_31 (.clk(clock_1_out), .D(out_20), .Q(out_21));  // open: Qn, preset, en, reset
  D_Flip_Flop d_ff_32 (.clk(clock_1_out), .D(out_30), .Q(out_31));  // open: Qn, preset, en, reset
endmodule

module Register_File (
  input  [31:0] Dato_de_Entrada,
  input  in_2,
  input  [31:0] Salida_High_Low,
  input  in_4,
  input  [31:0] High,
  input  [31:0] Low,
  input  H_L_Enable,
  input  [31:0] Salida_B,
  input  [31:0] Salida_A,
  input  Enable,
  input  [4:0] in_11,
  input  [4:0] in_12,
  input  [4:0] Register_Address
);

  wire Clock, R1, R2, R3, R4, R5, R6, R7, R8, R9, R10, R11, R12, R13, R14, R15, R16, R17, R18, R19, R20, R21,
       R22, R23, R24, R25, R26, R27, R28, R29, R30, R31;
  wire [31:0] H, L, S0, S1, S2, S3, S4, S5, S6, S7, S8, S9, S10, S11, S12, S13, S14, S15, S16, S17, S18, S19,
       S20, S21, S22, S23, S24, S25, S26, S27, S28, S29, S30, S31;

  Clock clock_1 (.out(Clock));
  Demultiplexer #(.select(5), .enable("false")) demultiplexer_1 (
    .out0(R1), .out1(R2), .out2(R3), .out3(R4), .out4(R5), .out5(R6), .out6(R7), .out7(R8), .out8(R9),
    .out9(R10), .out10(R11), .out11(R12), .out12(R13), .out13(R14), .out14(R15), .out15(R16), .out16(R16),
    .out17(R17), .out18(R18), .out19(R19), .out20(R20), .out21(R21), .out22(R22), .out23(R23), .out24(R24),
    .out25(R25), .out26(R26), .out27(R27), .out28(R28), .out29(R29), .out30(R30), .out31(R31), .in(Enable),
    .sel(Register_Address));
  Register #(.width(32)) register_1 (.Q(S0));  // open: D, en, clk, clr
  Register #(.width(32)) register_2 (.D(Dato_de_Entrada), .en(R8), .Q(S8), .clk(Clock), .clr(in_2));
  Register #(.width(32)) register_3 (.D(Dato_de_Entrada), .en(R16), .Q(S16), .clk(Clock), .clr(in_2));
  Register #(.width(32)) register_4 (.D(Dato_de_Entrada), .en(R24), .Q(S24), .clk(Clock), .clr(in_2));
  Register #(.width(32)) register_5 (.D(Dato_de_Entrada), .en(R1), .Q(S1), .clk(Clock), .clr(in_2));
  Register #(.width(32)) register_6 (.D(Dato_de_Entrada), .en(R9), .Q(S9), .clk(Clock), .clr(in_2));
  Register #(.width(32)) register_7 (.D(Dato_de_Entrada), .en(R17), .Q(S17), .clk(Clock), .clr(in_2));
  Register #(.width(32)) register_8 (.D(Dato_de_Entrada), .en(R25), .Q(S25), .clk(Clock), .clr(in_2));
  Register #(.width(32)) register_9 (.D(Dato_de_Entrada), .en(R2), .Q(S2), .clk(Clock), .clr(in_2));
  Register #(.width(32)) register_10 (.D(Dato_de_Entrada), .en(R10), .Q(S10), .clk(Clock), .clr(in_2));
  Register #(.width(32)) register_11 (.D(Dato_de_Entrada), .en(R18), .Q(S18), .clk(Clock), .clr(in_2));
  Register #(.width(32)) register_12 (.D(Dato_de_Entrada), .en(R26), .Q(S26), .clk(Clock), .clr(in_2));
  Register #(.width(32)) register_13 (.D(Dato_de_Entrada), .en(R3), .Q(S3), .clk(Clock), .clr(in_2));
  Register #(.width(32)) register_14 (.D(Dato_de_Entrada), .en(R11), .Q(S11), .clk(Clock), .clr(in_2));
  Register #(.width(32)) register_15 (.D(Dato_de_Entrada), .en(R19), .Q(S19), .clk(Clock), .clr(in_2));
  Register #(.width(32)) register_16 (.D(Dato_de_Entrada), .en(R27), .Q(S27), .clk(Clock), .clr(in_2));
  Register #(.width(32)) register_17 (.D(Dato_de_Entrada), .en(R4), .Q(S4), .clk(Clock), .clr(in_2));
  Register #(.width(32)) register_18 (.D(Dato_de_Entrada), .en(R12), .Q(S12), .clk(Clock), .clr(in_2));
  Register #(.width(32)) register_19 (.D(Dato_de_Entrada), .en(R20), .Q(S20), .clk(Clock), .clr(in_2));
  Register #(.width(32)) register_20 (.D(Dato_de_Entrada), .en(R28), .Q(S28), .clk(Clock), .clr(in_2));
  Register #(.width(32)) register_21 (.D(Dato_de_Entrada), .en(R5), .Q(S5), .clk(Clock), .clr(in_2));
  Register #(.width(32)) register_22 (.D(Dato_de_Entrada), .en(R13), .Q(S13), .clk(Clock), .clr(in_2));
  Register #(.width(32)) register_23 (.D(Dato_de_Entrada), .en(R21), .Q(S21), .clk(Clock), .clr(in_2));
  Register #(.width(32)) register_24 (.D(Dato_de_Entrada), .en(R29), .Q(S29), .clk(Clock), .clr(in_2));
  Register #(.width(32)) register_25 (.D(Dato_de_Entrada), .en(R6), .Q(S6), .clk(Clock), .clr(in_2));
  Register #(.width(32)) register_26 (.D(Dato_de_Entrada), .en(R14), .Q(S14), .clk(Clock), .clr(in_2));
  Register #(.width(32)) register_27 (.D(Dato_de_Entrada), .en(R22), .Q(S22), .clk(Clock), .clr(in_2));
  Register #(.width(32)) register_28 (.D(Dato_de_Entrada), .en(R30), .Q(S30), .clk(Clock), .clr(in_2));
  Multiplexer #(.select(5), .width(32), .enable("false")) multiplexer_1 (
    .in0(S0), .in1(S1), .in2(S2), .in3(S3), .in4(S4), .in5(S5), .in6(S6), .in7(S7), .in8(S8), .in9(S9),
    .in10(S10), .in11(S11), .in12(S12), .in13(S13), .in14(S14), .in15(S15), .in16(S16), .in17(S17),
    .in18(S18), .in19(S19), .in20(S20), .in21(S21), .in22(S22), .in23(S23), .in24(S24), .in25(S25),
    .in26(S26), .in27(S27), .in28(S28), .in29(S29), .in30(S30), .in31(S31), .out(Salida_A), .sel(in_12));
  Register #(.width(32)) register_29 (.D(Dato_de_Entrada), .en(R7), .Q(S7), .clk(Clock), .clr(in_2));
  Register #(.width(32)) register_30 (.D(Dato_de_Entrada), .en(R15), .Q(S15), .clk(Clock), .clr(in_2));
  Register #(.width(32)) register_31 (.D(Dato_de_Entrada), .en(R23), .Q(S23), .clk(Clock), .clr(in_2));
  Register #(.width(32)) register_32 (.D(Dato_de_Entrada), .en(R31), .Q(S31), .clk(Clock), .clr(in_2));
  Register #(.width(32)) register_33 (.D(High), .en(H_L_Enable), .Q(H), .clk(Clock), .clr(in_2));
  Multiplexer #(.width(32), .enable("false")) multiplexer_2 (.in0(H), .in1(L), .out(Salida_High_Low), .sel(in_4));
  Register #(.width(32)) register_34 (.D(Low), .en(H_L_Enable), .Q(L), .clk(Clock), .clr(in_2));
  Multiplexer #(.select(5), .width(32), .enable("false")) multiplexer_3 (
    .in0(S0), .in1(S1), .in2(S2), .in3(S3), .in4(S4), .in5(S5), .in6(S6), .in7(S7), .in8(S8), .in9(S9),
    .in10(S10), .in11(S11), .in12(S12), .in13(S13), .in14(S14), .in15(S15), .in16(S16), .in17(S17),
    .in18(S18), .in19(S19), .in20(S20), .in21(S21), .in22(S22), .in23(S23), .in24(S24), .in25(S25),
    .in26(S26), .in27(S27), .in28(S28), .in29(S29), .in30(S30), .in31(S31), .out(Salida_B), .sel(in_11));

  // Other names for the same wires on the sheet: DE[31:0] = Dato_de_Entrada; H_L = H_L_Enable; Reset = in_2
endmodule
