// Logisim project s-mips.circ as structural Verilog: 17 circuits, main circuit S-MIPS Board
module S_MIPS_Board (
  input  DESHABILITAR_DISPATCHER,
  output halt
);

  wire button_1_out, CLK, CS, d_ff_1_q, LCLR, LoadRAM, LoadRAMOn, LW, R_R_W, R_W, ram_dispatcher_1_finished,
       RCS, Reset_out, RST, TTY_EN;
  wire [2:0] KDB;
  wire [3:0] LMask, Mask, ram_1_read_time, ram_1_write_time, RMask;
  wire [6:0] KDB_DATA, TTY_DATA;
  wire [15:0] Addr, LAddr, RAddr;
  wire [31:0] I0, I1, I2, I3, LData, ram_1_data_out_0, ram_1_data_out_1, ram_1_data_out_2, ram_1_data_out_3,
       RI0, RI1, RI2, RI3;

  TTY #(.rows(25), .cols(80)) tty_1 (.data(TTY_DATA), .clk(CLK), .we(TTY_EN), .clr(RST));
  not not_1 (LoadRAMOn, ram_dispatcher_1_finished);
  RAM_Dispatcher ram_dispatcher_1 (
    .WriteTime(ram_1_write_time), .Clock(CLK), .Data(LData), .Address(LAddr), .Mask(LMask),
    .Finished(ram_dispatcher_1_finished), .Write(LW), .CLR(LCLR));
  Keyboard #(.buflen(64)) keyboard_1 (.clk(CLK), .re(KDB[0]), .avail(KDB[2]), .data(KDB_DATA));  // open: clr
  RAM ram_1 (
    .Address(RAddr), .Data_Out_0(ram_1_data_out_0), .Data_Out_1(ram_1_data_out_1),
    .Data_Out_2(ram_1_data_out_2), .Data_Out_3(ram_1_data_out_3), .Data_In_0(RI0), .Data_In_1(RI1),
    .Data_In_2(RI2), .Data_In_3(RI3), .Mask(RMask), .nRead_Write(R_R_W), .Chip_Select(RCS),
    .Read_Time(ram_1_read_time), .Reset(button_1_out), .Write_Time(ram_1_write_time));
  Button button_1 (.out(button_1_out));
  D_Flip_Flop d_ff_1 (.clk(CLK), .D(1'b1), .Q(d_ff_1_q), .reset(Reset_out));  // open: Qn, preset, en
  Button Reset (.out(Reset_out));
  S_MIPS s_mips_1 (
    .Kbd_Enable(KDB[0]), .Address(Addr), .Kbd_Clear(KDB[1]), .Kbd_Available(KDB[2]), .RAM_In_0(I0),
    .Kbd_ASCII_Data(KDB_DATA), .RAM_In_1(I1), .TTY_Enable(TTY_EN), .RAM_In_2(I2), .RAM_In_3(I3),
    .TTY_ASCII_Data(TTY_DATA), .Reset(RST), .RAM_Out_0(ram_1_data_out_0), .Clock(CLK),
    .RAM_Out_1(ram_1_data_out_1), .Stop(halt), .RAM_Out_2(ram_1_data_out_2), .RAM_Out_3(ram_1_data_out_3),
    .Mask(Mask), .Read_Time(ram_1_read_time), .Write_Time(ram_1_write_time), .nRead_Write(R_W),
    .Chip_Select(CS));
  D_Flip_Flop d_ff_2 (.clk(CLK), .D(d_ff_1_q), .Qn(LCLR), .reset(Reset_out));  // open: Q, preset, en
  or or_1 (RST, LCLR, LoadRAM);
  Clock clock_1 (.out(CLK));
  Multiplexer #(.width(32), .enable("false")) multiplexer_1 (.in0(I0), .in1(LData), .out(RI0), .sel(LoadRAM));
  Multiplexer #(.width(32), .enable("false")) multiplexer_2 (.in0(I1), .in1(LData), .out(RI1), .sel(LoadRAM));
  Multiplexer #(.width(32), .enable("false")) multiplexer_3 (.in0(I2), .in1(LData), .out(RI2), .sel(LoadRAM));
  Multiplexer #(.width(32), .enable("false")) multiplexer_4 (.in0(I3), .in1(LData), .out(RI3), .sel(LoadRAM));
  and and_1 (LoadRAM, ~DESHABILITAR_DISPATCHER, LoadRAMOn);  // AND_Gate
  Multiplexer #(.width(16), .enable("false")) multiplexer_5 (.in0(Addr), .in1(LAddr), .out(RAddr), .sel(LoadRAM));
  Multiplexer #(.width(4), .enable("false")) multiplexer_6 (.in0(Mask), .in1(LMask), .out(RMask), .sel(LoadRAM));
  Multiplexer #(.enable("false")) multiplexer_7 (.in0(CS), .in1(LW), .out(RCS), .sel(LoadRAM));
  Multiplexer #(.enable("false")) multiplexer_8 (.in0(R_W), .in1(LW), .out(R_R_W), .sel(LoadRAM));

  // Notes on the sheet:
  //   NO MODIFICAR
  //   Keyboard
endmodule

module RAM (
  input  [15:0] Address,
  input  [31:0] Data_In_0,
  input  [31:0] Data_In_1,
  input  [31:0] Data_In_2,
  input  [31:0] Data_In_3,
  input  [3:0] Mask,
  input  nRead_Write,
  input  Chip_Select,
  input  Reset,
  output [31:0] Data_Out_0,
  output [31:0] Data_Out_1,
  output [31:0] Data_Out_2,
  output [31:0] Data_Out_3,
  output [3:0] Read_Time,
  output [3:0] Write_Time
);

  wire and_2_out, and_3_out, and_4_out, and_5_out, and_6_out, and_7_out, and_8_out, and_9_out, Changed, CLK,
       comparator_2_eq, comparator_3_eq, comparator_4_eq, comparator_5_eq, comparator_6_eq, Count,
       demultiplexer_3_out0, Idle, Idle_q, Load, Load0, Load1, nand_1_out, or_1_out, or_2_out, or_3_out,
       or_4_out, or_5_out, or_6_out, or_7_out, or_8_out, or_9_out, or_10_out, Proc_q, Update_Mem, Zero_Time;
  wire [3:0] counter_1_q, multiplexer_1_out, subtractor_1_out;
  wire [31:0] register_1_q, register_2_q, register_3_q, register_4_q, register_5_q;

  // Probe on 4'b0011
  // Probe on 4'b0010
  Multiplexer #(.width(4), .enable("false")) multiplexer_1 (
    .in0(4'b0011), .in1(4'b0010), .out(multiplexer_1_out), .sel(nRead_Write));
  or or_1 (or_1_out, Idle, Update_Mem);
  or or_2 (or_2_out, ~Chip_Select, Reset);  // OR_Gate
  Subtractor #(.width(4)) subtractor_1 (.a(multiplexer_1_out), .b(4'b0010), .out(subtractor_1_out));  // open: bin, bout
  D_Flip_Flop u_Idle (.clk(CLK), .D(or_1_out), .Q(Idle_q), .preset(or_2_out));  // open: Qn, en, reset
  Demultiplexer #(.enable("false")) demultiplexer_1 (.out0(Idle), .out1(Load0), .in(Idle_q), .sel(Changed));
  // Probe on counter_1_q
  Counter #(.width(4), .max('hf)) counter_1 (
    .load(Load), .D(subtractor_1_out), .count(Count), .Q(counter_1_q), .clk(CLK), .clr(or_3_out));  // open: carry
  or or_3 (or_3_out, ~Chip_Select, Reset);  // OR_Gate
  Comparator #(.width(4), .mode("unsigned")) comparator_1 (
    .a(4'b0000), .b(counter_1_q), .eq(Zero_Time));  // open: gt, lt
  or or_4 (or_4_out, Count, Load0, Load1);
  Register #(.width(32)) register_1 (.D(Data_In_0), .en(Chip_Select), .Q(register_1_q), .clk(CLK), .clr(or_5_out));
  or or_5 (or_5_out, ~Chip_Select, Reset);  // OR_Gate
  Register #(.width(32)) register_2 (.D(Data_In_1), .en(Chip_Select), .Q(register_2_q), .clk(CLK), .clr(or_6_out));
  or or_6 (or_6_out, ~Chip_Select, Reset);  // OR_Gate
  Register #(.width(32)) register_3 (.D(Data_In_2), .en(Chip_Select), .Q(register_3_q), .clk(CLK), .clr(or_7_out));
  or or_7 (or_7_out, ~Chip_Select, Reset);  // OR_Gate
  Register #(.width(32)) register_4 (.D(Data_In_3), .en(Chip_Select), .Q(register_4_q), .clk(CLK), .clr(or_8_out));
  or or_8 (or_8_out, ~Chip_Select, Reset);  // OR_Gate
  Register #(.width(32)) register_5 (
    .D({{11{1'b1}}, nRead_Write, Mask, Address}), .en(Chip_Select), .Q(register_5_q), .clk(CLK),
    .clr(or_9_out));
  or or_9 (or_9_out, ~Chip_Select, Reset);  // OR_Gate
  D_Flip_Flop Proc (.clk(CLK), .D(or_4_out), .Q(Proc_q), .reset(or_10_out));  // open: Qn, preset, en
  or or_10 (or_10_out, ~Chip_Select, Reset);  // OR_Gate
  Demultiplexer #(.enable("false")) demultiplexer_2 (
    .out0(Count), .out1(Update_Mem), .in(demultiplexer_3_out0), .sel(Zero_Time));
  Demultiplexer #(.enable("false")) demultiplexer_3 (
    .out0(demultiplexer_3_out0), .out1(Load1), .in(Proc_q), .sel(Changed));
  Clock clock_1 (.out(CLK));
  Comparator #(.width(32)) comparator_2 (.a(register_1_q), .b(Data_In_0), .eq(comparator_2_eq));  // open: gt, lt
  Comparator #(.width(32)) comparator_3 (.a(register_2_q), .b(Data_In_1), .eq(comparator_3_eq));  // open: gt, lt
  Comparator #(.width(32)) comparator_4 (.a(register_3_q), .b(Data_In_2), .eq(comparator_4_eq));  // open: gt, lt
  Comparator #(.width(32)) comparator_5 (.a(register_4_q), .b(Data_In_3), .eq(comparator_5_eq));  // open: gt, lt
  Comparator #(.width(32)) comparator_6 (
    .a(register_5_q), .b({{11{1'b1}}, nRead_Write, Mask, Address}), .eq(comparator_6_eq));  // open: gt, lt
  nand nand_1 (nand_1_out, comparator_6_eq, comparator_2_eq, comparator_3_eq, comparator_4_eq, comparator_5_eq);
  and and_1 (Changed, nand_1_out, Chip_Select);
  or or_11 (Load, Count, Load1, Load0);
  and and_2 (and_2_out, Mask[0], Update_Mem, nRead_Write);
  and and_3 (and_3_out, Mask[1], Update_Mem, nRead_Write);
  and and_4 (and_4_out, Mask[2], Update_Mem, nRead_Write);
  and and_5 (and_5_out, Mask[3], Update_Mem, nRead_Write);
  RAM_part #(.addrWidth(16), .dataWidth(32), .bus("separate")) ram_1 (
    .addr(Address), .din(Data_In_0), .data(Data_Out_0), .str(and_2_out), .sel(Chip_Select), .clk(CLK),
    .ld(and_6_out), .clr(Reset));
  and and_6 (and_6_out, ~nRead_Write, Idle);  // AND_Gate
  RAM_part #(.addrWidth(16), .dataWidth(32), .bus("separate")) ram_2 (
    .addr(Address), .din(Data_In_1), .data(Data_Out_1), .str(and_3_out), .sel(Chip_Select), .clk(CLK),
    .ld(and_7_out), .clr(Reset));
  and and_7 (and_7_out, ~nRead_Write, Idle);  // AND_Gate
  RAM_part #(.addrWidth(16), .dataWidth(32), .bus("separate")) ram_3 (
    .addr(Address), .din(Data_In_2), .data(Data_Out_2), .str(and_4_out), .sel(Chip_Select), .clk(CLK),
    .ld(and_8_out), .clr(Reset));
  and and_8 (and_8_out, ~nRead_Write, Idle);  // AND_Gate
  RAM_part #(.addrWidth(16), .dataWidth(32), .bus("separate")) ram_4 (
    .addr(Address), .din(Data_In_3), .data(Data_Out_3), .str(and_5_out), .sel(Chip_Select), .clk(CLK),
    .ld(and_9_out), .clr(Reset));
  and and_9 (and_9_out, ~nRead_Write, Idle);  // AND_Gate

  assign Read_Time = 4'b0011;
  assign Write_Time = 4'b0010;

  // Other names for the same wires on the sheet: M0 = Mask[0]; M1 = Mask[1]; M2 = Mask[2]; M3 = Mask[3];
  //   RW = nRead_Write; CLR = Reset; CS = Chip_Select; Load2 = Count

  // Notes on the sheet:
  //   NO MODIFICAR
  //   excepto quizás los valores RT y WT
  //   BANK0
  //   BANK1
  //   BANK2
  //   BANK3
endmodule

module S_MIPS (
  input  Kbd_Available,
  input  [6:0] Kbd_ASCII_Data,
  input  [31:0] RAM_Out_0,
  input  [31:0] RAM_Out_1,
  input  Reset,
  input  [31:0] RAM_Out_2,
  input  Clock,
  input  [31:0] RAM_Out_3,
  input  [3:0] Read_Time,
  input  [3:0] Write_Time,
  output Kbd_Enable,
  output [15:0] Address,
  output Kbd_Clear,
  output TTY_Enable,
  output [6:0] TTY_ASCII_Data,
  output Stop,
  output [31:0] RAM_In_0,
  output [31:0] RAM_In_1,
  output [31:0] RAM_In_2,
  output [31:0] RAM_In_3,
  output [3:0] Mask,
  output nRead_Write,
  output Chip_Select
);

  wire EN_SP, Hi_Lo_Op, Inm_Op, KBD_DATA_PATH, load_instruction, load_pc, Log_Inm_Op, lw, M_D_OP, mflhi, pop,
       R_W, RAM_Ope, \rand , Stack_Op, Unsigned;
  wire [1:0] OFFSET;
  wire [2:0] Branch_Ope;
  wire [3:0] ALU_Ope;
  wire [5:0] Func_code, Op_Code;
  wire [31:0] KBD_DATA1, multiplexer_1_out, To_RAM;

  assign KBD_DATA1 = {{25{Kbd_ASCII_Data[6]}}, Kbd_ASCII_Data};  // Bit_Extender bit_extender_1
  Multiplexer #(.width(32), .enable("false")) multiplexer_1 (
    .in0({32{1'b1}}), .in1(KBD_DATA1), .out(multiplexer_1_out), .sel(Kbd_Enable));
  Control_Unit control_unit_1 (
    .Op_code(Op_Code), .Func_code(Func_code), .Read_Time(Read_Time), .Write_Time(Write_Time), .Clk(Clock),
    .Reset(Reset), .ALU_Ope(ALU_Ope), .Branch_Ope(Branch_Ope), .Inmediate_Ope(Inm_Op), .M_D_OP(M_D_OP),
    .Logical_Inmediate_Ope(Log_Inm_Op), .Hi_Lo_Ope(Hi_Lo_Op), .mfhi(mflhi), .Rand(\rand ),
    .KBD_DP(KBD_DATA_PATH), .lw(lw), .Stack_Ope(Stack_Op), .pop(pop), .SP(EN_SP), .KBD_ENABLE(Kbd_Enable),
    .TTY_ENABLE(TTY_Enable), .Chip_Select(Chip_Select), .RW_RAM(nRead_Write), .Load_PC(load_pc), .END(Stop),
    .Load_Instuction(load_instruction), .Unsigned(Unsigned), .R___W(R_W), .RAM_Ope(RAM_Ope));
  Data_Path data_path_1 (
    .Bank_0(RAM_Out_0), .Bank_1(RAM_Out_1), .Bank_2(RAM_Out_2), .Bank_3(RAM_Out_3),
    .KBD_DATA(multiplexer_1_out), .ALU_Ope(ALU_Ope), .Branch_Ope(Branch_Ope), .CLK(Clock), .Reset(Reset),
    .Load_PC(load_pc), .Load_Instruction(load_instruction), .R___W(R_W), .Inmediate_Operation(Inm_Op),
    .Logical_Inmediate(Log_Inm_Op), .Hi_Lo_Ope(Hi_Lo_Op), .mfhi_mflo(mflhi), .RAM_Ope(RAM_Ope), .lw(lw),
    .Stack_Ope(Stack_Op), .pop(pop), .En_SP(EN_SP), .Hight_Op(M_D_OP), .Unsigned(Unsigned),
    .KBD_E(KBD_DATA_PATH), .Rand(\rand ), .To_Ram(To_RAM), .Address(Address), .Op_Code(Op_Code),
    .Func_code(Func_code), .TTY(TTY_ASCII_Data), .Offset(OFFSET), .Mask_prime(Mask));  // open: Zero_Div
  Demultiplexer #(.select(2), .width(32), .enable("false")) demultiplexer_1 (
    .out0(RAM_In_0), .out1(RAM_In_1), .out2(RAM_In_2), .out3(RAM_In_3), .in(To_RAM), .sel(OFFSET));

  assign Kbd_Clear = Reset;

  // Other names for the same wires on the sheet: CLK = Clock; CS = Chip_Select; KBD_AVAIL = Kbd_Available;
  //   CLR = Reset; KBD_CLR = Reset; KBD_DATA[6:0] = Kbd_ASCII_Data; RAM_A[15:0] = Address;
  //   RAM_INPUT_0[31:0] = RAM_In_0; RAM_INPUT_1[31:0] = RAM_In_1; RAM_INPUT_2[31:0] = RAM_In_2;
  //   RAM_INPUT_3[31:0] = RAM_In_3; RAM_MASK[3:0] = Mask; RAM_OUTPUT_0[31:0] = RAM_Out_0;
  //   RAM_OUTPUT_1[31:0] = RAM_Out_1; RAM_OUTPUT_2[31:0] = RAM_Out_2; RAM_OUTPUT_3[31:0] = RAM_Out_3;
  //   RW = nRead_Write; RW_RAM = nRead_Write; TTY_DATA[6:0] = TTY_ASCII_Data

  // Notes on the sheet:
  //   RAM ADDRESS
  //   DATA FROM RAM
  //   DATA TO RAM
  //   DATA WRITE MASK
  //   RAM TIMING
  //   RAM CONTROL
  //   KEYBOARD
  //   TTY
  //   SEQUENCING
endmodule

module RAM_Dispatcher (
  input  [3:0] WriteTime,
  input  Clock,
  input  CLR,
  output [31:0] Data,
  output [15:0] Address,
  output [3:0] Mask,
  output Finished,
  output Write
);

  wire demultiplexer_2_out1, demultiplexer_3_out1, End, IDLE_q, IncAddr, Load, or_1_out, or_2_out, While_q,
       WriteEnd;
  wire [3:0] counter_1_q;
  wire [31:0] CurrentAddress_q;

  Counter #(.width(32), .max('hffffffff)) CurrentAddress (
    .count(IncAddr), .Q({CurrentAddress_q[31:18], Address, CurrentAddress_q[1:0]}), .clk(Clock), .clr(CLR));  // open: load, D, carry
  or or_1 (or_1_out, IncAddr, demultiplexer_3_out1, Finished);
  D_Flip_Flop IDLE (.clk(Clock), .D(or_1_out), .Q(IDLE_q), .preset(CLR));  // open: Qn, en, reset
  Demultiplexer #(.enable("false")) demultiplexer_1 (.out0(Load), .out1(Finished), .in(IDLE_q), .sel(End));
  D_Flip_Flop While (.clk(Clock), .D(or_2_out), .Q(While_q), .reset(CLR));  // open: Qn, preset, en
  or or_2 (or_2_out, Write, Load);
  RAM_part #(.addrWidth(18), .dataWidth(32)) ram_1 (
    .addr({Address, CurrentAddress_q[1:0]}), .data(Data), .clk(Clock));  // open: sel, ld, clr
  Demultiplexer #(.enable("false")) demultiplexer_2 (
    .out0(Write), .out1(demultiplexer_2_out1), .in(While_q), .sel(WriteEnd));
  Decoder #(.select(2)) decoder_1 (
    .out0(Mask[0]), .out1(Mask[1]), .out2(Mask[2]), .out3(Mask[3]), .sel(CurrentAddress_q[1:0]));  // open: en
  Demultiplexer #(.enable("false")) demultiplexer_3 (
    .out0(IncAddr), .out1(demultiplexer_3_out1), .in(demultiplexer_2_out1), .sel(End));
  Counter #(.width(4), .max('hf)) counter_1 (
    .load(Load), .D(WriteTime), .count(Write), .Q(counter_1_q), .clk(Clock));  // open: carry, clr
  Comparator #(.width(32)) comparator_1 (.a(Data), .b({32{1'b1}}), .eq(End));  // open: gt, lt
  Comparator #(.width(4)) comparator_2 (.a(4'b0000), .b(counter_1_q), .eq(WriteEnd));  // open: gt, lt

  // Other names for the same wires on the sheet: CLK = Clock; Count = Write; WT[3:0] = WriteTime
endmodule

module Control_Unit (
  input  [5:0] Op_code,
  input  [5:0] Func_code,
  input  [3:0] Read_Time,
  input  [3:0] Write_Time,
  input  Clk,
  input  Reset,
  output [3:0] ALU_Ope,
  output [2:0] Branch_Ope,
  output Inmediate_Ope,
  output M_D_OP,
  output Logical_Inmediate_Ope,
  output Hi_Lo_Ope,
  output mfhi,
  output Rand,
  output KBD_DP,
  output lw,
  output Stack_Ope,
  output pop,
  output SP,
  output KBD_ENABLE,
  output TTY_ENABLE,
  output Chip_Select,
  output RW_RAM,
  output Load_PC,
  output END,
  output Load_Instuction,
  output Unsigned,
  output R___W,
  output RAM_Ope
);

  wire CS_0, CS_1, CS_2, CS_3, CS_4, d_ff_1_q, d_ff_3_q, d_ff_8_q, demultiplexer_1_out0,
       demultiplexer_1_out1, demultiplexer_2_out0, demultiplexer_3_out0, demultiplexer_3_out4,
       demultiplexer_3_out5, demultiplexer_3_out6, demultiplexer_4_out0, demultiplexer_4_out1,
       demultiplexer_5_out1, demultiplexer_6_out0, demultiplexer_7_out0, demultiplexer_7_out1,
       demultiplexer_8_out0, demultiplexer_9_out0, demultiplexer_9_out1, demultiplexer_10_out0, IDLE_q, lw_t,
       nor_1_out, not_1_out, or_7_out, or_8_out, or_9_out, or_10_out, or_11_out, or_12_out, pop_t, R___W_1,
       SP2, Wait, WAIT_q;
  wire [1:0] Sp_Ope;
  wire [2:0] CU_Ope;
  wire [3:0] counter_1_q, RT____WT;

  Multiplexer #(.width(4), .enable("false")) multiplexer_1 (
    .in0(Read_Time), .in1(Write_Time), .out(RT____WT), .sel(RW_RAM));
  or or_1 (Chip_Select, CS_0, CS_1, CS_4, CS_2, CS_3);
  or or_2 (RW_RAM, CS_1, CS_4);
  Operation_Decoder operation_decoder_1 (
    .Op_code(Op_code), .Func_code(Func_code), .CU_Operation(CU_Ope), .ALU_Operation(ALU_Ope),
    .Branch_Operation(Branch_Ope), .Special_Ope(Sp_Ope), .pop(pop_t), .mfhi(mfhi), .lw(lw_t),
    .Logical_Inme_Ope(Logical_Inmediate_Ope), .Unsigned(Unsigned), .M_D_OP(M_D_OP));
  D_Flip_Flop d_ff_1 (.clk(Clk), .D(Chip_Select), .Q(d_ff_1_q), .reset(Reset));  // open: Qn, preset, en
  or or_3 (R___W, R___W_1, Inmediate_Ope, Hi_Lo_Ope, lw, pop, KBD_DP, Rand);
  Counter #(.width(4), .max('hf)) counter_1 (
    .load(Chip_Select), .D(RT____WT), .count(d_ff_1_q), .Q(counter_1_q), .clk(Clk));  // open: carry, clr
  nor nor_1 (nor_1_out, counter_1_q[0], counter_1_q[1], counter_1_q[2], counter_1_q[3]);
  and and_1 (Wait, nor_1_out, d_ff_1_q);
  or or_4 (Stack_Ope, CS_4, CS_3);
  or or_5 (RAM_Ope, CS_1, CS_2);
  or or_6 (SP, pop, SP2);
  D_Flip_Flop IDLE (.clk(Clk), .D(demultiplexer_1_out0), .Q(IDLE_q), .preset(Reset));  // open: Qn, en, reset
  Demultiplexer #(.disabled(0), .enable("false")) demultiplexer_1 (
    .out0(demultiplexer_1_out0), .out1(demultiplexer_1_out1), .in(IDLE_q), .sel(not_1_out));
  not not_1 (not_1_out, Reset);
  or or_7 (or_7_out, demultiplexer_2_out0, d_ff_8_q, demultiplexer_1_out1);
  D_Flip_Flop d_ff_2 (.clk(Clk), .D(or_7_out), .Q(CS_0), .reset(Reset));  // open: Qn, preset, en
  Demultiplexer #(.enable("false")) demultiplexer_2 (
    .out0(demultiplexer_2_out0), .out1(Load_Instuction), .in(CS_0), .sel(Wait));
  D_Flip_Flop d_ff_3 (.clk(Clk), .D(Load_Instuction), .Q(d_ff_3_q), .reset(Reset));  // open: Qn, preset, en
  Demultiplexer #(.select(3), .disabled(0), .enable("false")) demultiplexer_3 (
    .out0(demultiplexer_3_out0), .out1(R___W_1), .out2(Inmediate_Ope), .out3(Hi_Lo_Ope),
    .out4(demultiplexer_3_out4), .out5(demultiplexer_3_out5), .out6(demultiplexer_3_out6), .in(d_ff_3_q),
    .sel(CU_Ope));  // open: out7
  Demultiplexer #(.disabled(0), .enable("false")) demultiplexer_4 (
    .out0(demultiplexer_4_out0), .out1(demultiplexer_4_out1), .in(demultiplexer_3_out4), .sel(lw_t));
  Demultiplexer #(.disabled(0), .enable("false")) demultiplexer_5 (
    .out0(SP2), .out1(demultiplexer_5_out1), .in(demultiplexer_3_out5), .sel(pop_t));
  Demultiplexer #(.select(2), .disabled(0), .enable("false")) demultiplexer_6 (
    .out0(demultiplexer_6_out0), .out1(Rand), .out2(KBD_DP), .out3(TTY_ENABLE), .in(demultiplexer_3_out6),
    .sel(Sp_Ope));
  or or_8 (or_8_out, demultiplexer_7_out0, demultiplexer_4_out0);
  or or_9 (or_9_out, demultiplexer_8_out0, demultiplexer_4_out1);
  or or_10 (or_10_out, demultiplexer_9_out0, SP2);
  or or_11 (or_11_out, demultiplexer_10_out0, demultiplexer_5_out1);
  D_Flip_Flop u_END (.clk(Clk), .D(or_12_out), .Q(END), .reset(Reset));  // open: Qn, preset, en
  or or_12 (or_12_out, END, demultiplexer_6_out0);
  D_Flip_Flop d_ff_4 (.clk(Clk), .D(or_8_out), .Q(CS_1), .reset(Reset));  // open: Qn, preset, en
  D_Flip_Flop d_ff_5 (.clk(Clk), .D(or_9_out), .Q(CS_2), .reset(Reset));  // open: Qn, preset, en
  D_Flip_Flop d_ff_6 (.clk(Clk), .D(or_10_out), .Q(CS_4), .reset(Reset));  // open: Qn, preset, en
  D_Flip_Flop d_ff_7 (.clk(Clk), .D(or_11_out), .Q(CS_3), .reset(Reset));  // open: Qn, preset, en
  Demultiplexer #(.enable("false")) demultiplexer_7 (
    .out0(demultiplexer_7_out0), .out1(demultiplexer_7_out1), .in(CS_1), .sel(Wait));
  Demultiplexer #(.enable("false")) demultiplexer_8 (.out0(demultiplexer_8_out0), .out1(lw), .in(CS_2), .sel(Wait));
  Demultiplexer #(.enable("false")) demultiplexer_9 (
    .out0(demultiplexer_9_out0), .out1(demultiplexer_9_out1), .in(CS_4), .sel(Wait));
  Demultiplexer #(.enable("false")) demultiplexer_10 (.out0(demultiplexer_10_out0), .out1(pop), .in(CS_3), .sel(Wait));
  D_Flip_Flop u_WAIT (.clk(Clk), .D(TTY_ENABLE), .Q(WAIT_q), .reset(Reset));  // open: Qn, preset, en
  D_Flip_Flop WAIT_2 (.clk(Clk), .D(KBD_DP), .Q(KBD_ENABLE), .reset(Reset));  // open: Qn, preset, en
  or or_13 (Load_PC, demultiplexer_3_out0, R___W_1, Inmediate_Ope, Hi_Lo_Ope, demultiplexer_7_out1, Rand, lw, demultiplexer_9_out1, pop, KBD_ENABLE, WAIT_q);
  D_Flip_Flop d_ff_8 (.clk(Clk), .D(Load_PC), .Q(d_ff_8_q), .reset(Reset));  // open: Qn, preset, en

  // Other names for the same wires on the sheet: CS = Chip_Select; Load_Inst = Load_Instuction;
  //   Logical_Inme_Ope = Logical_Inmediate_Ope; Inmedaite = Inmediate_Ope; R___W_2 = Inmediate_Ope;
  //   R___W_3 = Hi_Lo_Ope; R___W_5 = KBD_DP; R___W_6 = Rand; R_W = R___W; RAM_Op = RAM_Ope; R_W_RAM_1 = CS_1;
  //   RAM_Ope_1 = CS_1; RAM_Ope_2 = CS_2; RT[3:0] = Read_Time; R___W_7 = lw; S_lw = lw; R___W_4 = pop; S_pop = pop;
  //   SP1 = pop; Stack_OP = Stack_Ope; R_W_RAM_2 = CS_4; Stack_Ope_1 = CS_4; Stack_Ope_2 = CS_3; WT[3:0] = Write_Time

  // Notes on the sheet:
  //   Input
  //   Ope-Func Decode
  //   DISJUNCTION
  //   Wait
  //   Branch Operation
  //   ALU Operation
  //   Special Operation
  //   Inmediate Operation
  //   Register Operation
  //   RAM Operation
  //   Stack Operation
  //   Store word
  //   Load word
  //   Push
  //   Pop
  //   Output
endmodule

module Operation_Decoder (
  input  [5:0] Op_code,
  input  [5:0] Func_code,
  output [2:0] CU_Operation,
  output [3:0] ALU_Operation,
  output [2:0] Branch_Operation,
  output [1:0] Special_Ope,
  output pop,
  output mfhi,
  output lw,
  output Logical_Inme_Ope,
  output Unsigned,
  output M_D_OP
);

  wire add, addi, AL_ope, \and , and_5_out, and_6_out, and_7_out, and_8_out, and_9_out, and_10_out,
       and_17_out, and_18_out, and_19_out, and_20_out, and_21_out, and_22_out, and_29_out, and_30_out,
       and_31_out, and_35_out, and_36_out, and_39_out, and_40_out, and_41_out, and_42_out, and_59_out,
       and_63_out, andi, beq, bgtz, blez, bltz, bne, Branch_Ope, div, divu, F_000000, halt, Inme_Ope, j, jr,
       kbd, mflo, mult, mulu, nop, \nor , O_000000, O_111000, O_111111, \or , or_11_out, or_12_out,
       or_13_out, or_14_out, or_15_out, or_16_out, or_17_out, ori, push, RAM_Ope, Registers_Ope, rnd, sliti,
       slitiu, slt, sltu, Special_Ope_t, Stack_Ope, sub, sw, tty, \xor , xori;

  and and_1 (O_000000, ~Op_code[0], ~Op_code[1], ~Op_code[2], ~Op_code[3], ~Op_code[4], ~Op_code[5]);  // AND_Gate
  and and_2 (O_111000, ~Op_code[0], ~Op_code[1], ~Op_code[2], Op_code[3], Op_code[4], Op_code[5]);  // AND_Gate
  and and_3 (O_111111, Op_code[0], Op_code[1], Op_code[2], Op_code[3], Op_code[4], Op_code[5]);
  and and_4 (F_000000, ~Func_code[0], ~Func_code[1], ~Func_code[2], ~Func_code[3], ~Func_code[4], ~Func_code[5]);  // AND_Gate
  and and_5 (and_5_out, ~Func_code[0], ~Func_code[1], ~Func_code[2], ~Func_code[3], ~Func_code[4], Func_code[5]);  // AND_Gate
  and and_6 (and_6_out, ~Func_code[0], Func_code[1], ~Func_code[2], ~Func_code[3], ~Func_code[4], Func_code[5]);  // AND_Gate
  and and_7 (and_7_out, ~Func_code[0], ~Func_code[1], ~Func_code[2], Func_code[3], Func_code[4], ~Func_code[5]);  // AND_Gate
  and and_8 (and_8_out, Func_code[0], ~Func_code[1], ~Func_code[2], Func_code[3], Func_code[4], ~Func_code[5]);  // AND_Gate
  and and_9 (and_9_out, ~Func_code[0], Func_code[1], ~Func_code[2], Func_code[3], Func_code[4], ~Func_code[5]);  // AND_Gate
  and and_10 (and_10_out, Func_code[0], Func_code[1], ~Func_code[2], Func_code[3], Func_code[4], ~Func_code[5]);  // AND_Gate
  and and_11 (add, and_5_out, O_000000);
  and and_12 (sub, and_6_out, O_000000);
  and and_13 (mult, and_7_out, O_000000);
  and and_14 (mulu, and_8_out, O_000000);
  and and_15 (div, and_9_out, O_000000);
  and and_16 (divu, and_10_out, O_000000);
  and and_17 (and_17_out, ~Func_code[0], Func_code[1], ~Func_code[2], Func_code[3], ~Func_code[4], Func_code[5]);  // AND_Gate
  and and_18 (and_18_out, Func_code[0], Func_code[1], ~Func_code[2], Func_code[3], ~Func_code[4], Func_code[5]);  // AND_Gate
  and and_19 (and_19_out, ~Func_code[0], ~Func_code[1], Func_code[2], ~Func_code[3], ~Func_code[4], Func_code[5]);  // AND_Gate
  and and_20 (and_20_out, Func_code[0], ~Func_code[1], Func_code[2], ~Func_code[3], ~Func_code[4], Func_code[5]);  // AND_Gate
  and and_21 (and_21_out, Func_code[0], Func_code[1], Func_code[2], ~Func_code[3], ~Func_code[4], Func_code[5]);  // AND_Gate
  and and_22 (and_22_out, ~Func_code[0], ~Func_code[1], ~Func_code[2], Func_code[3], ~Func_code[4], Func_code[5]);  // AND_Gate
  and and_23 (slt, and_17_out, O_000000);
  and and_24 (sltu, and_18_out, O_000000);
  and and_25 (\and , and_19_out, O_000000);
  and and_26 (\or , and_20_out, O_000000);
  and and_27 (\nor , and_21_out, O_000000);
  and and_28 (\xor , and_22_out, O_000000);
  and and_29 (and_29_out, ~Func_code[0], ~Func_code[1], ~Func_code[2], Func_code[3], ~Func_code[4], ~Func_code[5]);  // AND_Gate
  and and_30 (and_30_out, ~Func_code[0], ~Func_code[1], ~Func_code[2], ~Func_code[3], Func_code[4], ~Func_code[5]);  // AND_Gate
  and and_31 (and_31_out, ~Func_code[0], Func_code[1], ~Func_code[2], ~Func_code[3], Func_code[4], ~Func_code[5]);  // AND_Gate
  and and_32 (jr, and_29_out, O_000000);
  and and_33 (mfhi, and_30_out, O_000000);
  and and_34 (mflo, and_31_out, O_000000);
  and and_35 (and_35_out, ~Func_code[0], ~Func_code[1], ~Func_code[2], ~Func_code[3], ~Func_code[4], ~Func_code[5]);  // AND_Gate
  and and_36 (and_36_out, Func_code[0], ~Func_code[1], ~Func_code[2], ~Func_code[3], ~Func_code[4], ~Func_code[5]);  // AND_Gate
  and and_37 (pop, and_35_out, O_111000);
  and and_38 (push, and_36_out, O_111000);
  and and_39 (and_39_out, Func_code[0], Func_code[1], Func_code[2], Func_code[3], Func_code[4], Func_code[5]);
  and and_40 (and_40_out, ~Func_code[0], Func_code[1], ~Func_code[2], ~Func_code[3], ~Func_code[4], ~Func_code[5]);  // AND_Gate
  and and_41 (and_41_out, ~Func_code[0], ~Func_code[1], Func_code[2], ~Func_code[3], ~Func_code[4], ~Func_code[5]);  // AND_Gate
  and and_42 (and_42_out, Func_code[0], ~Func_code[1], ~Func_code[2], ~Func_code[3], ~Func_code[4], ~Func_code[5]);  // AND_Gate
  and and_43 (halt, and_39_out, O_111111);
  and and_44 (rnd, and_40_out, O_111111);
  and and_45 (kbd, and_41_out, O_111111);
  and and_46 (tty, and_42_out, O_111111);
  and and_47 (addi, ~Op_code[0], ~Op_code[1], ~Op_code[2], Op_code[3], ~Op_code[4], ~Op_code[5]);  // AND_Gate
  and and_48 (sliti, ~Op_code[0], Op_code[1], ~Op_code[2], Op_code[3], ~Op_code[4], ~Op_code[5]);  // AND_Gate
  and and_49 (slitiu, Op_code[0], Op_code[1], ~Op_code[2], Op_code[3], ~Op_code[4], ~Op_code[5]);  // AND_Gate
  and and_50 (andi, ~Op_code[0], ~Op_code[1], Op_code[2], Op_code[3], ~Op_code[4], ~Op_code[5]);  // AND_Gate
  and and_51 (ori, Op_code[0], ~Op_code[1], Op_code[2], Op_code[3], ~Op_code[4], ~Op_code[5]);  // AND_Gate
  and and_52 (xori, ~Op_code[0], Op_code[1], Op_code[2], Op_code[3], ~Op_code[4], ~Op_code[5]);  // AND_Gate
  and and_53 (beq, ~Op_code[0], ~Op_code[1], Op_code[2], ~Op_code[3], ~Op_code[4], ~Op_code[5]);  // AND_Gate
  and and_54 (bne, Op_code[0], ~Op_code[1], Op_code[2], ~Op_code[3], ~Op_code[4], ~Op_code[5]);  // AND_Gate
  and and_55 (blez, ~Op_code[0], Op_code[1], Op_code[2], ~Op_code[3], ~Op_code[4], ~Op_code[5]);  // AND_Gate
  and and_56 (bgtz, Op_code[0], Op_code[1], Op_code[2], ~Op_code[3], ~Op_code[4], ~Op_code[5]);  // AND_Gate
  and and_57 (bltz, Op_code[0], ~Op_code[1], ~Op_code[2], ~Op_code[3], ~Op_code[4], ~Op_code[5]);  // AND_Gate
  and and_58 (j, ~Op_code[0], Op_code[1], ~Op_code[2], ~Op_code[3], ~Op_code[4], ~Op_code[5]);  // AND_Gate
  and and_59 (and_59_out, ~Op_code[0], ~Op_code[1], ~Op_code[2], ~Op_code[3], ~Op_code[4], ~Op_code[5]);  // AND_Gate
  and and_60 (nop, and_59_out, F_000000);
  and and_61 (lw, Op_code[0], Op_code[1], ~Op_code[2], ~Op_code[3], ~Op_code[4], Op_code[5]);  // AND_Gate
  and and_62 (sw, Op_code[0], Op_code[1], ~Op_code[2], Op_code[3], ~Op_code[4], Op_code[5]);  // AND_Gate
  or or_1 (Logical_Inme_Ope, andi, ori, xori);
  or or_2 (Special_Ope_t, halt, rnd, kbd, tty);
  or or_3 (Stack_Ope, pop, push);
  or or_4 (RAM_Ope, lw, sw);
  or or_5 (Registers_Ope, mfhi, mflo);
  or or_6 (AL_ope, add, sub, mult, mulu, div, divu, slt, sltu, \and , \or , \nor , \xor );
  or or_7 (Branch_Ope, nop, beq, bne, blez, bgtz, bltz, j, jr);
  or or_8 (Inme_Ope, addi, sliti, slitiu, andi, ori, xori);
  or or_9 (M_D_OP, mult, mulu, div, divu);
  or or_10 (Unsigned, mult, div);
  or or_11 (or_11_out, add, addi);
  or or_12 (or_12_out, \and , andi);
  or or_13 (or_13_out, \or , ori);
  or or_14 (or_14_out, \xor , xori);
  or or_15 (or_15_out, slt, sliti);
  or or_16 (or_16_out, sltu, slitiu);
  and and_63 (and_63_out, ~AL_ope, ~Inme_Ope);  // AND_Gate
  or or_17 (or_17_out, halt, 1'b1);
  Priority_Encoder #(.select(2), .disabled(0)) priority_encoder_1 (
    .in0(or_17_out), .in1(rnd), .in2(kbd), .in3(tty), .out(Special_Ope), .en_in(1'b1));  // open: gs, en_out
  Priority_Encoder #(.disabled(0)) priority_encoder_2 (
    .in0(Branch_Ope), .in1(AL_ope), .in2(Inme_Ope), .in3(Registers_Ope), .in4(RAM_Ope), .in5(Stack_Ope),
    .in6(Special_Ope_t), .out(CU_Operation), .en_in(1'b1));  // open: in7, gs, en_out
  Priority_Encoder #(.select(4), .disabled(0)) priority_encoder_3 (
    .in0(or_11_out), .in1(sub), .in2(mult), .in3(mulu), .in4(div), .in5(divu), .in6(or_12_out),
    .in7(or_13_out), .in8(\nor ), .in9(or_14_out), .in10(or_15_out), .in11(or_16_out), .in15(and_63_out),
    .out(ALU_Operation), .en_in(1'b1));  // open: in12, in13, in14, gs, en_out
  Priority_Encoder #(.disabled(0)) priority_encoder_4 (
    .in0(1'b1), .in1(beq), .in2(bne), .in3(blez), .in4(bgtz), .in5(bltz), .in6(j), .in7(jr),
    .out(Branch_Operation), .en_in(1'b1));  // open: gs, en_out

  // Other names for the same wires on the sheet: Mult_Div_Ope = M_D_OP

  // Notes on the sheet:
  //   Input
  //   CODES
  //   ALU
  //   OPERATIONS(FUNC CODE)
  //   Register
  //   Stack
  //   Special
  //   ALU
  //   OP CODE DECODE
  //   BRANCH
  //   RAM
  //   CLASIFICATION(OPERATIONS)
  //   Output/Encode Op
  //   Control Unit
  //   ALU
  //   Branch
  //   Special
  //   Others  Operations
endmodule

module Data_Path (
  input  [31:0] Bank_0,
  input  [31:0] Bank_1,
  input  [31:0] Bank_2,
  input  [31:0] Bank_3,
  input  [31:0] KBD_DATA,
  input  [3:0] ALU_Ope,
  input  [2:0] Branch_Ope,
  input  CLK,
  input  Reset,
  input  Load_PC,
  input  Load_Instruction,
  input  R___W,
  input  Inmediate_Operation,
  input  Logical_Inmediate,
  input  Hi_Lo_Ope,
  input  mfhi_mflo,
  input  RAM_Ope,
  input  lw,
  input  Stack_Ope,
  input  pop,
  input  En_SP,
  input  Hight_Op,
  input  Unsigned,
  input  KBD_E,
  input  Rand,
  output [31:0] To_Ram,
  output [15:0] Address,
  output [5:0] Op_Code,
  output [5:0] Func_code,
  output [6:0] TTY,
  output [1:0] Offset,
  output [3:0] Mask_prime,
  output Zero_Div
);

  wire and_1_out, C_Add, C_Rest, or_1_out, Rs_____Rt, Rs_____Rt_t, Rs____Rt;
  wire [4:0] multiplexer_5_out, Rd, Rs, Rt, x;
  wire [15:0] Constant;
  wire [25:0] Destiny_Jump;
  wire [31:0] bit_extender_1_out, bit_extender_2_out, High, High_ALU, Instr, Low, Low_ALU, multiplexer_1_out,
       multiplexer_2_out, multiplexer_3_out, multiplexer_4_out, multiplexer_6_out, multiplexer_7_out,
       multiplexer_8_out, multiplexer_9_out, multiplexer_11_out, PC, PC_N, random_1_out, Register_Data, Rt_t,
       SP;
  wire [31:7] Rs_t;

  Multiplexer #(.select(2), .width(32), .disabled(0), .enable("false")) multiplexer_1 (
    .in0(Bank_0), .in1(Bank_1), .in2(Bank_2), .in3(Bank_3), .out(multiplexer_1_out), .sel(Offset));
  Program_Counter program_counter_1 (.PC(PC), .ENABLE(Load_PC), .CLCK(CLK), .RESET(Reset), .NEXT_PC(PC_N));
  Next_Adress next_adress_1 (
    .PC(PC_N), .CONSTANT(Constant), .CHOSEN_R({Rs_t, TTY}), .SP(SP), .STACK(Stack_Ope), .RAM(RAM_Ope),
    .ADRESS(Address), .OFFSET(Offset), .MASK(Mask_prime));
  Branch_Control branch_control_1 (
    .Rs({Rs_t, TTY}), .PC_in(PC_N), .\const (Constant), .Jump(Destiny_Jump), .Branch_Operation(Branch_Ope),
    .Rs_____Rt(Rs_____Rt_t), .PC_Out(PC));
  Little_Endian little_endian_1 (.Input(multiplexer_1_out), .Output(Instr));
  Instruction_Decoder instruction_decoder_1 (
    .Input(Instr), .Load(Load_Instruction), .CLCK(CLK), .RESET(Reset), .OP_CODE(Op_Code),
    .JUMP(Destiny_Jump), .CONSTANT(Constant), .FUNC_CODE(Func_code), .RS(Rs), .RT(Rt), .RD(Rd), .X(x));
  Multiplexer #(.width(32), .disabled(0), .enable("false")) multiplexer_2 (
    .in0(Low), .in1(High), .out(multiplexer_2_out), .sel(mfhi_mflo));
  assign bit_extender_1_out = {{16{Constant[15]}}, Constant};  // Bit_Extender bit_extender_1
  assign bit_extender_2_out = {{16{1'b0}}, Constant};  // Bit_Extender bit_extender_2
  Multiplexer #(.width(32), .disabled(0), .enable("false")) multiplexer_3 (
    .in0(bit_extender_1_out), .in1(bit_extender_2_out), .out(multiplexer_3_out), .sel(Logical_Inmediate));
  Multiplexer #(.width(32), .disabled(0), .enable("false")) multiplexer_4 (
    .in0(Low_ALU), .in1(multiplexer_2_out), .out(multiplexer_4_out), .sel(Hi_Lo_Ope));
  or or_1 (or_1_out, Inmediate_Operation, RAM_Ope);
  Multiplexer #(.width(5), .disabled(0), .enable("false")) multiplexer_5 (
    .in0(Rd), .in1(Rt), .out(multiplexer_5_out), .sel(or_1_out));
  Multiplexer #(.width(32), .disabled(0), .enable("false")) multiplexer_6 (
    .in0(Rt_t), .in1(multiplexer_3_out), .out(multiplexer_6_out), .sel(Inmediate_Operation));
  Multiplexer #(.width(32), .disabled(0), .enable("false")) multiplexer_7 (
    .in0(multiplexer_4_out), .in1(Instr), .out(multiplexer_7_out), .sel(lw));
  and and_1 (and_1_out, R___W, ~Hight_Op);  // AND_Gate
  Multiplexer #(.width(32), .disabled(0), .enable("false")) multiplexer_8 (
    .in0(multiplexer_7_out), .in1(Instr), .out(multiplexer_8_out), .sel(pop));
  ALU alu_1 (
    .Rs({Rs_t, TTY}), .Rt(multiplexer_6_out), .Select_Op(ALU_Ope), .Hight_Op(Hight_Op), .Unsigned(Unsigned),
    .Shoosed(Low_ALU), .Hight(High_ALU), .Great(Rs____Rt), .Equal(Rs_____Rt_t), .Less(Rs_____Rt),
    .C_Add(C_Add), .C_Rest(C_Rest), .Div_x_0(Zero_Div));
  Multiplexer #(.width(32), .disabled(0), .enable("false")) multiplexer_9 (
    .in0(multiplexer_8_out), .in1(KBD_DATA), .out(multiplexer_9_out), .sel(KBD_E));
  Random #(.width(32)) random_1 (.clk(CLK), .out(random_1_out));  // open: next, clr
  Register_File register_file_1 (
    .Dato_de_Entrada(Register_Data), .High(High_ALU), .Low(Low_ALU), .Register_Address(multiplexer_5_out),
    .SA(Rs), .SB(Rt), .CLCK(CLK), .RESET(Reset), .R_W(and_1_out), .En_SP(En_SP), .pop(pop),
    .H_L_Enable(Hight_Op), .Salida_A({Rs_t, TTY}), .Salida_B(Rt_t), .Salida_Low(Low), .Salida_High(High),
    .SP(SP));
  Multiplexer #(.width(32), .disabled(0), .enable("false")) multiplexer_10 (
    .in0(multiplexer_9_out), .in1(random_1_out), .out(Register_Data), .sel(Rand));
  Multiplexer #(.width(32), .disabled(0), .enable("false")) multiplexer_11 (
    .in0(Rt_t), .in1({Rs_t, TTY}), .out(multiplexer_11_out), .sel(Stack_Ope));
  Little_Endian little_endian_2 (.Input(multiplexer_11_out), .Output(To_Ram));

  // Other names for the same wires on the sheet: Inme = Inmediate_Operation; KBD = KBD_E;
  //   Load_instr = Load_Instruction; Logical_Inme = Logical_Inmediate; Mask[3:0] = Mask_prime; mfhi = mfhi_mflo;
  //   OpHight = Hight_Op; Random = Rand; Rs_t[6:0] = TTY; RST = Reset

  // Notes on the sheet:
  //   INPUT
  //   Processing
  //   OUTPUT
endmodule

module ALU (
  input  [31:0] Rs,
  input  [31:0] Rt,
  input  [3:0] Select_Op,
  input  Hight_Op,
  input  Unsigned,
  output [31:0] Shoosed,
  output [31:0] Hight,
  output Great,
  output Equal,
  output Less,
  output C_Add,
  output C_Rest,
  output Div_x_0
);

  wire LessU, OpHight;
  wire [31:0] ADD, AND, DIV, Divu, Mult, multiplexer_3_out, multiplexer_4_out, Mulu, NOR, OR, R_Div, R_Divu,
       R_Mult, R_Mulu, Slt, Sltu, SUB, XOR;

  assign AND = Rs & Rt;  // AND_Gate and_1, 32 bits wide
  assign OR = Rs | Rt;  // OR_Gate or_1, 32 bits wide
  assign XOR = Rs ^ Rt;  // XOR_Gate xor_1, 32 bits wide
  assign NOR = ~(Rs | Rt);  // NOR_Gate nor_1, 32 bits wide
  Adder #(.width(32)) adder_1 (.a(Rs), .b(Rt), .out(ADD), .cin(1'b0), .cout(C_Add));
  Subtractor #(.width(32)) subtractor_1 (.a(Rs), .b(Rt), .out(SUB), .bin(1'b0), .bout(C_Rest));
  Divider #(.width(32)) divider_1 (.a(Rs), .b(Rt), .out(Divu), .rem(R_Divu));  // open: upper
  Comparator #(.width(32)) comparator_1 (.a(Rs), .b(Rt), .gt(Great), .eq(Equal), .lt(Less));
  Multiplexer #(.width(32), .enable("false")) multiplexer_1 (.in0({32{1'b0}}), .in1(32'h1), .out(Slt), .sel(Less));
  Multiplier #(.width(32)) multiplier_1 (.a(Rs), .b(Rt), .out(Mulu), .cout(R_Mulu));  // open: cin
  Comparator #(.width(32), .mode("unsigned")) comparator_2 (.a(Rs), .b(Rt), .lt(LessU));  // open: gt, eq
  Multiplexer #(.width(32), .enable("false")) multiplexer_2 (.in0({32{1'b0}}), .in1(32'h1), .out(Sltu), .sel(LessU));
  Mulu mulu_1 (.A(Rs), .B(Rt), .Output_Low(Mult), .High(R_Mult));
  Divu divu_1 (.A(Rs), .B(Rt), .Output_Low(DIV), .High(R_Div));
  Multiplexer #(.width(32), .enable("false")) multiplexer_3 (
    .in0(R_Mult), .in1(R_Mulu), .out(multiplexer_3_out), .sel(Unsigned));
  Multiplexer #(.width(32), .enable("false")) multiplexer_4 (
    .in0(R_Div), .in1(R_Divu), .out(multiplexer_4_out), .sel(Unsigned));
  Multiplexer #(.select(4), .width(32), .enable("false")) multiplexer_5 (
    .in0(ADD), .in1(SUB), .in2(Mult), .in3(Mulu), .in4(Divu), .in5(DIV), .in6(AND), .in7(OR), .in8(NOR),
    .in9(XOR), .in10(Slt), .in11(Sltu), .out(Shoosed), .sel(Select_Op));  // open: in12, in13, in14, in15
  Multiplexer #(.width(32), .enable("false")) multiplexer_6 (
    .in0(multiplexer_3_out), .in1(multiplexer_4_out), .out(Hight), .sel(OpHight));
  Comparator #(.width(32), .mode("unsigned")) comparator_3 (.a(Rt), .b({32{1'b0}}), .eq(Div_x_0));  // open: gt, lt

  // Other names for the same wires on the sheet: A[31:0] = Rs; B[31:0] = Rt; D0 = Div_x_0; Hi_S[31:0] = Hight;
  //   OpHight_t = Hight_Op

  // Notes on the sheet:
  //   Entradas
  //   Logical Operations
  //   Comparers
  //   Aritmetic Operations
  //   General Shooser
  //   Hight Shooser
  //   Cero Div
  //   Exits
  //   Flags
endmodule

module Instruction_Decoder (
  input  [31:0] Input,
  input  Load,
  input  CLCK,
  input  RESET,
  output [5:0] OP_CODE,
  output [25:0] JUMP,
  output [15:0] CONSTANT,
  output [5:0] FUNC_CODE,
  output [4:0] RS,
  output [4:0] RT,
  output [4:0] RD,
  output [4:0] X
);

  Register #(.width(32)) Instruction (
    .D(Input), .en(Load), .Q({OP_CODE, JUMP[25:16], CONSTANT}), .clk(CLCK), .clr(RESET));

  assign FUNC_CODE = CONSTANT[5:0];
  assign JUMP[15:0] = CONSTANT;
  assign RD = CONSTANT[15:11];
  assign RS = JUMP[25:21];
  assign RT = JUMP[20:16];
  assign X = CONSTANT[10:6];

  // Other names for the same wires on the sheet: CLK = CLCK;
  //   Final_Instruction[31:0] = {OP_CODE, JUMP[25:16], CONSTANT}; Instruction[31:0] = Input

  // Notes on the sheet:
  //   INPUT
  //   LOADING
  //   SEPARATION
  //   OUTPUT
endmodule

module Program_Counter (
  input  [31:0] PC,
  input  ENABLE,
  input  CLCK,
  input  RESET,
  output [31:0] NEXT_PC
);

  Register #(.width(32)) LOADING_PC (.D(PC), .en(ENABLE), .Q(NEXT_PC), .clk(CLCK), .clr(RESET));

  // Notes on the sheet:
  //   INPUT
  //   LOADING
  //   OUTPUT
endmodule

module Next_Adress (
  input  [31:0] PC,
  input  [15:0] CONSTANT,
  input  [31:0] CHOSEN_R,
  input  [31:0] SP,
  input  STACK,
  input  RAM,
  output [15:0] ADRESS,
  output [1:0] OFFSET,
  output [3:0] MASK
);

  wire [31:0] bit_extender_1_out, CR___CNST, multiplexer_1_out;

  assign bit_extender_1_out = {{16{CONSTANT[15]}}, CONSTANT};  // Bit_Extender bit_extender_1
  Adder #(.width(32)) adder_1 (.a(CHOSEN_R), .b(bit_extender_1_out), .out(CR___CNST));  // open: cin, cout
  Multiplexer #(.select(2), .width(32), .enable("false")) multiplexer_1 (
    .in0(PC), .in1(SP), .in2(CR___CNST),
    .out({multiplexer_1_out[31:20], ADRESS, OFFSET, multiplexer_1_out[1:0]}), .sel({RAM, STACK}));  // open: in3
  Demultiplexer #(.select(2), .enable("false")) demultiplexer_1 (
    .out0(MASK[0]), .out1(MASK[1]), .out2(MASK[2]), .out3(MASK[3]), .in(1'b1), .sel(OFFSET));

  // Other names for the same wires on the sheet: STACK_O = STACK; RAM_O = RAM; CNST[15:0] = CONSTANT

  // Notes on the sheet:
  //   INPUT
  //   CALCULATION
  //   OUTPUT
endmodule

module Branch_Control (
  input  [31:0] Rs,
  input  [31:0] PC_in,
  input  [15:0] \const ,
  input  [25:0] Jump,
  input  [2:0] Branch_Operation,
  input  Rs_____Rt,
  output [31:0] PC_Out
);

  wire and_1_out, and_2_out, and_3_out, and_4_out, and_5_out, b_jump, beq, bgtz, blez, bltz, bne,
       comparator_1_eq, comparator_1_lt, j, jr, nop, Rs____0, Rs_____0;
  wire [1:0] jump_t;
  wire [2:0] Branch_Ope;
  wire [31:0] bit_extender_1_out, Branch, multiplier_1_out, Standart;
  wire [31:28] J_PC;

  Decoder #(.select(3), .disabled(0), .enable("false")) decoder_1 (
    .out0(nop), .out1(beq), .out2(bne), .out3(blez), .out4(bgtz), .out5(bltz), .out6(j), .out7(jr),
    .sel(Branch_Ope));
  Priority_Encoder #(.select(2)) priority_encoder_1 (
    .in0(1'b1), .in1(b_jump), .in2(j), .in3(jr), .out(jump_t), .en_in(1'b1));  // open: gs, en_out
  Adder #(.width(32)) adder_1 (.a(PC_in), .b(32'h4), .out(Standart));  // open: cin, cout
  assign bit_extender_1_out = {{16{\const [15]}}, \const };  // Bit_Extender bit_extender_1
  BitSelector #(.width(32), .group(4)) bitselector_1 (.in(PC_in), .out(J_PC), .sel(3'b111));
  Comparator #(.width(32)) comparator_1 (
    .a(Rs), .b({32{1'b0}}), .eq(comparator_1_eq), .lt(comparator_1_lt));  // open: gt
  Comparator #(.width(32)) comparator_2 (.a(Rs), .b({32{1'b0}}), .lt(Rs____0));  // open: gt, eq
  Multiplier #(.width(32)) multiplier_1 (.a(32'h4), .b(bit_extender_1_out), .out(multiplier_1_out));  // open: cin, cout
  or or_1 (Rs_____0, comparator_1_eq, comparator_1_lt);
  and and_1 (and_1_out, beq, Rs_____Rt);
  and and_2 (and_2_out, bne, ~Rs_____Rt);  // AND_Gate
  and and_3 (and_3_out, blez, Rs_____0);
  and and_4 (and_4_out, bgtz, ~Rs_____0);  // AND_Gate
  and and_5 (and_5_out, bltz, Rs____0);
  Adder #(.width(32)) adder_2 (.a(Standart), .b(multiplier_1_out), .out(Branch));  // open: cin, cout
  or or_2 (b_jump, and_1_out, and_2_out, and_3_out, and_4_out, and_5_out);
  Multiplexer #(.select(2), .width(32), .disabled(0), .enable("false")) multiplexer_1 (
    .in0(Standart), .in1(Branch), .in2({J_PC, Jump, 2'b00}), .in3(Rs), .out(PC_Out), .sel(jump_t));

  // Other names for the same wires on the sheet: Branch_Ope_t[2:0] = Branch_Operation; J_PC[27:2] = Jump

  // Notes on the sheet:
  //   INPUT
  //   OPERATION DECODE
  //   JUMP ENCODE
  //   Standart Value
  //   Branch Value
  //   J Jump 
  //   B Jump 
  //   Choose Jump
  //   Output
endmodule

module Little_Endian (
  input  [31:0] Input,
  output [31:0] Output
);


  assign Output = {Input[7:0], Input[15:8], Input[23:16], Input[31:24]};
endmodule

module Register_File (
  input  [31:0] Dato_de_Entrada,
  input  [31:0] High,
  input  [31:0] Low,
  input  [4:0] Register_Address,
  input  [4:0] SA,
  input  [4:0] SB,
  input  CLCK,
  input  RESET,
  input  R_W,
  input  En_SP,
  input  pop,
  input  H_L_Enable,
  output [31:0] Salida_A,
  output [31:0] Salida_B,
  output [31:0] Salida_Low,
  output [31:0] Salida_High,
  output [31:0] SP
);

  wire demultiplexer_1_out0, or_1_out, R1, R2, R3, R4, R5, R6, R7, R8, R9, R10, R11, R12, R13, R14, R15, R16,
       R17, R18, R19, R20, R21, R22, R23, R24, R25, R26, R27, R28, R29, R30, R31;
  wire [31:0] adder_1_out, multiplexer_3_out, S0, S1, S2, S3, S4, S5, S6, S7, S8, S9, S10, S11, S12, S13,
       S14, S15, S16, S17, S18, S19, S20, S21, S22, S23, S24, S25, S26, S27, S28, S29, S30, SP_t,
       subtractor_1_out;

  Register #(.width(32)) register_1 (.D(Dato_de_Entrada), .en(1'b0), .Q(S0), .clk(CLCK), .clr(RESET));
  Register #(.width(32)) register_2 (.D(Dato_de_Entrada), .en(R8), .Q(S8), .clk(CLCK), .clr(RESET));
  Register #(.width(32)) register_3 (.D(Dato_de_Entrada), .en(R16), .Q(S16), .clk(CLCK), .clr(RESET));
  Register #(.width(32)) register_4 (.D(Dato_de_Entrada), .en(R24), .Q(S24), .clk(CLCK), .clr(RESET));
  Register #(.width(32)) register_5 (.D(Dato_de_Entrada), .en(R1), .Q(S1), .clk(CLCK), .clr(RESET));
  Register #(.width(32)) register_6 (.D(Dato_de_Entrada), .en(R9), .Q(S9), .clk(CLCK), .clr(RESET));
  Register #(.width(32)) register_7 (.D(Dato_de_Entrada), .en(R17), .Q(S17), .clk(CLCK), .clr(RESET));
  Register #(.width(32)) register_8 (.D(Dato_de_Entrada), .en(R25), .Q(S25), .clk(CLCK), .clr(RESET));
  Subtractor #(.width(32)) subtractor_1 (.a(SP), .b(32'h4), .out(subtractor_1_out));  // open: bin, bout
  Adder #(.width(32)) adder_1 (.a(SP), .b(32'h4), .out(adder_1_out));  // open: cin, cout
  Register #(.width(32)) register_9 (.D(Dato_de_Entrada), .en(R2), .Q(S2), .clk(CLCK), .clr(RESET));
  Multiplexer #(.width(32), .disabled(0), .enable("false")) multiplexer_1 (
    .in0(subtractor_1_out), .in1(adder_1_out), .out(SP_t), .sel(pop));
  Register #(.width(32)) register_10 (.D(Dato_de_Entrada), .en(R10), .Q(S10), .clk(CLCK), .clr(RESET));
  Register #(.width(32)) register_11 (.D(Dato_de_Entrada), .en(R18), .Q(S18), .clk(CLCK), .clr(RESET));
  Register #(.width(32)) register_12 (.D(Dato_de_Entrada), .en(R26), .Q(S26), .clk(CLCK), .clr(RESET));
  Multiplexer #(.select(5), .width(32), .enable("false")) multiplexer_2 (
    .in0(S0), .in1(S1), .in2(S2), .in3(S3), .in4(S4), .in5(S5), .in6(S6), .in7(S7), .in8(S8), .in9(S9),
    .in10(S10), .in11(S11), .in12(S12), .in13(S13), .in14(S14), .in15(S15), .in16(S16), .in17(S17),
    .in18(S18), .in19(S19), .in20(S20), .in21(S21), .in22(S22), .in23(S23), .in24(S24), .in25(S25),
    .in26(S26), .in27(S27), .in28(S28), .in29(S29), .in30(S30), .in31(SP), .out(Salida_A), .sel(SA));
  Register #(.width(32)) register_13 (.D(Dato_de_Entrada), .en(R3), .Q(S3), .clk(CLCK), .clr(RESET));
  Register #(.width(32)) register_14 (.D(Dato_de_Entrada), .en(R11), .Q(S11), .clk(CLCK), .clr(RESET));
  Register #(.width(32)) register_15 (.D(Dato_de_Entrada), .en(R19), .Q(S19), .clk(CLCK), .clr(RESET));
  Register #(.width(32)) register_16 (.D(Dato_de_Entrada), .en(R27), .Q(S27), .clk(CLCK), .clr(RESET));
  Multiplexer #(.width(32), .disabled(0), .enable("false")) multiplexer_3 (
    .in0(Dato_de_Entrada), .in1(SP_t), .out(multiplexer_3_out), .sel(En_SP));
  or or_1 (or_1_out, En_SP, R31);
  Register #(.width(32)) u_SP (.D(multiplexer_3_out), .en(or_1_out), .Q(SP), .clk(CLCK), .clr(RESET));
  Register #(.width(32)) register_17 (.D(Dato_de_Entrada), .en(R4), .Q(S4), .clk(CLCK), .clr(RESET));
  Register #(.width(32)) register_18 (.D(Dato_de_Entrada), .en(R12), .Q(S12), .clk(CLCK), .clr(RESET));
  Register #(.width(32)) register_19 (.D(Dato_de_Entrada), .en(R20), .Q(S20), .clk(CLCK), .clr(RESET));
  Register #(.width(32)) register_20 (.D(Dato_de_Entrada), .en(R28), .Q(S28), .clk(CLCK), .clr(RESET));
  Register #(.width(32)) register_21 (.D(Dato_de_Entrada), .en(R5), .Q(S5), .clk(CLCK), .clr(RESET));
  Register #(.width(32)) register_22 (.D(Dato_de_Entrada), .en(R13), .Q(S13), .clk(CLCK), .clr(RESET));
  Register #(.width(32)) register_23 (.D(Dato_de_Entrada), .en(R21), .Q(S21), .clk(CLCK), .clr(RESET));
  Register #(.width(32)) register_24 (.D(Dato_de_Entrada), .en(R29), .Q(S29), .clk(CLCK), .clr(RESET));
  Register #(.width(32)) register_25 (.D(High), .en(H_L_Enable), .Q(Salida_High), .clk(CLCK), .clr(RESET));
  Register #(.width(32)) register_26 (.D(Dato_de_Entrada), .en(R6), .Q(S6), .clk(CLCK), .clr(RESET));
  Register #(.width(32)) register_27 (.D(Dato_de_Entrada), .en(R14), .Q(S14), .clk(CLCK), .clr(RESET));
  Register #(.width(32)) register_28 (.D(Dato_de_Entrada), .en(R22), .Q(S22), .clk(CLCK), .clr(RESET));
  Register #(.width(32)) register_29 (.D(Dato_de_Entrada), .en(R30), .Q(S30), .clk(CLCK), .clr(RESET));
  Register #(.width(32)) register_30 (.D(Low), .en(H_L_Enable), .Q(Salida_Low), .clk(CLCK), .clr(RESET));
  Register #(.width(32)) register_31 (.D(Dato_de_Entrada), .en(R7), .Q(S7), .clk(CLCK), .clr(RESET));
  Register #(.width(32)) register_32 (.D(Dato_de_Entrada), .en(R15), .Q(S15), .clk(CLCK), .clr(RESET));
  Register #(.width(32)) register_33 (.D(Dato_de_Entrada), .en(R23), .Q(S23), .clk(CLCK), .clr(RESET));
  Multiplexer #(.select(5), .width(32), .enable("false")) multiplexer_4 (
    .in0(S0), .in1(S1), .in2(S2), .in3(S3), .in4(S4), .in5(S5), .in6(S6), .in7(S7), .in8(S8), .in9(S9),
    .in10(S10), .in11(S11), .in12(S12), .in13(S13), .in14(S14), .in15(S15), .in16(S16), .in17(S17),
    .in18(S18), .in19(S19), .in20(S20), .in21(S21), .in22(S22), .in23(S23), .in24(S24), .in25(S25),
    .in26(S26), .in27(S27), .in28(S28), .in29(S29), .in30(S30), .in31(SP), .out(Salida_B), .sel(SB));
  Demultiplexer #(.select(5), .enable("false")) demultiplexer_1 (
    .out0(demultiplexer_1_out0), .out1(R1), .out2(R2), .out3(R3), .out4(R4), .out5(R5), .out6(R6), .out7(R7),
    .out8(R8), .out9(R9), .out10(R10), .out11(R11), .out12(R12), .out13(R13), .out14(R14), .out15(R15),
    .out16(R16), .out17(R17), .out18(R18), .out19(R19), .out20(R20), .out21(R21), .out22(R22), .out23(R23),
    .out24(R24), .out25(R25), .out26(R26), .out27(R27), .out28(R28), .out29(R29), .out30(R30), .out31(R31),
    .in(R_W), .sel(Register_Address));
  // also tied to GND on the sheet: demultiplexer_1_out0

  // Other names for the same wires on the sheet: A[31:0] = Salida_A; Adress[4:0] = Register_Address;
  //   B[31:0] = Salida_B; Clock = CLCK; DE[31:0] = Dato_de_Entrada; H[31:0] = Salida_High; H_L = H_L_Enable;
  //   L[31:0] = Salida_Low; QSP[31:0] = SP; W = R_W

  // Notes on the sheet:
  //   INPUT
  //   Selector A
  //   Selector B
  //   Stack Pointer
  //   32Bits Registers(31)
  //   Choose Outputs A&B
  //   HI/LO
  //   Choose Register
  //   OUTPUT
endmodule

module Mulu (
  input  [31:0] A,
  input  [31:0] B,
  output [31:0] Output_Low,
  output [31:0] High
);

  wire [1:0] bitselector_2_out, bitselector_4_out;
  wire [31:0] C2, C2_t, c____C2, c____C2_t, c_minus_minus, c_minus_plus, c_plus_minus, c_plus_plus,
       negator_1_out, negator_2_out, negator_3_out, negator_4_out, tunnel, tunnel_t, tunnel_t_t, tunnel_t_t_t;

  Negator #(.width(32)) negator_1 (.in(B), .out(negator_1_out));
  Negator #(.width(32)) negator_2 (.in(A), .out(negator_2_out));
  Negator #(.width(32)) negator_3 (.in(A), .out(negator_3_out));
  Negator #(.width(32)) negator_4 (.in(B), .out(negator_4_out));
  Multiplier #(.width(32)) multiplier_1 (.a(A), .b(B), .out(tunnel_t), .cout(c_plus_plus));  // open: cin
  Multiplier #(.width(32)) multiplier_2 (.a(A), .b(negator_1_out), .out(tunnel), .cout(c_plus_minus));  // open: cin
  Multiplier #(.width(32)) multiplier_3 (.a(negator_2_out), .b(B), .out(tunnel_t_t), .cout(c_minus_plus));  // open: cin
  Multiplier #(.width(32)) multiplier_4 (
    .a(negator_3_out), .b(negator_4_out), .out(tunnel_t_t_t), .cout(c_minus_minus));  // open: cin
  A2_MULT a2_mult_1 (.Low(tunnel), .High(c_plus_minus), .LowC2(C2), .HighC2(c____C2));
  A2_MULT a2_mult_2 (.Low(tunnel_t_t), .High(c_minus_plus), .LowC2(C2_t), .HighC2(c____C2_t));
  BitSelector #(.width(32)) bitselector_1 (.in(A), .out(bitselector_2_out[1]), .sel({5{1'b1}}));
  BitSelector #(.width(32)) bitselector_2 (.in(B), .out(bitselector_2_out[0]), .sel({5{1'b1}}));
  Multiplexer #(.select(2), .width(32), .disabled(0), .enable("false")) multiplexer_1 (
    .in0(tunnel_t), .in1(C2), .in2(C2_t), .in3(tunnel_t_t_t), .out(Output_Low), .sel(bitselector_2_out));
  Multiplexer #(.select(2), .width(32), .disabled(0), .enable("false")) multiplexer_2 (
    .in0(c_plus_plus), .in1(c____C2), .in2(c____C2_t), .in3(c_minus_minus), .out(High),
    .sel(bitselector_4_out));
  BitSelector #(.width(32)) bitselector_3 (.in(A), .out(bitselector_4_out[1]), .sel({5{1'b1}}));
  BitSelector #(.width(32)) bitselector_4 (.in(B), .out(bitselector_4_out[0]), .sel({5{1'b1}}));
endmodule

module Divu (
  input  [31:0] A,
  input  [31:0] B,
  output [31:0] Output_Low,
  output [31:0] High
);

  wire [1:0] bitselector_2_out, bitselector_4_out;
  wire [31:0] c_minus_minus, c_minus_plus, c_plus_minus, c_plus_plus, divider_2_out, divider_3_out,
       negator_1_out, negator_2_out, negator_3_out, negator_4_out, tunnel, tunnel_t, tunnel_t_t, tunnel_t_t_t;

  Divider #(.width(32)) divider_1 (.a(A), .b(B), .out(tunnel_t), .rem(c_plus_plus));  // open: upper
  Divider #(.width(32)) divider_2 (.a(A), .b(negator_1_out), .out(divider_2_out), .rem(c_plus_minus));  // open: upper
  Negator #(.width(32)) negator_1 (.in(B), .out(negator_1_out));
  Negator #(.width(32)) negator_2 (.in(A), .out(negator_2_out));
  Divider #(.width(32)) divider_3 (.a(negator_2_out), .b(B), .out(divider_3_out), .rem(c_minus_plus));  // open: upper
  Negator #(.width(32)) negator_3 (.in(A), .out(negator_3_out));
  Divider #(.width(32)) divider_4 (
    .a(negator_3_out), .b(negator_4_out), .out(tunnel_t_t_t), .rem(c_minus_minus));  // open: upper
  Negator #(.width(32)) negator_4 (.in(B), .out(negator_4_out));
  Negator #(.width(32)) negator_5 (.in(divider_2_out), .out(tunnel));
  Negator #(.width(32)) negator_6 (.in(divider_3_out), .out(tunnel_t_t));
  BitSelector #(.width(32)) bitselector_1 (.in(A), .out(bitselector_2_out[1]), .sel({5{1'b1}}));
  BitSelector #(.width(32)) bitselector_2 (.in(B), .out(bitselector_2_out[0]), .sel({5{1'b1}}));
  BitSelector #(.width(32)) bitselector_3 (.in(A), .out(bitselector_4_out[1]), .sel({5{1'b1}}));
  BitSelector #(.width(32)) bitselector_4 (.in(B), .out(bitselector_4_out[0]), .sel({5{1'b1}}));
  Multiplexer #(.select(2), .width(32), .disabled(0), .enable("false")) multiplexer_1 (
    .in0(tunnel_t), .in1(tunnel), .in2(tunnel_t_t), .in3(tunnel_t_t_t), .out(Output_Low),
    .sel(bitselector_2_out));
  Multiplexer #(.select(2), .width(32), .disabled(0), .enable("false")) multiplexer_2 (
    .in0(c_plus_plus), .in1(c_plus_minus), .in2(c_minus_plus), .in3(c_minus_minus), .out(High),
    .sel(bitselector_4_out));
endmodule

module A2_MULT (
  input  [31:0] Low,
  input  [31:0] High,
  output [31:0] LowC2,
  output [31:0] HighC2
);

  wire adder_1_cout;
  wire [31:0] not_1_out, not_2_out;

  assign not_1_out = ~Low;  // NOT_Gate not_1, 32 bits wide
  Adder #(.width(32)) adder_1 (.a(not_1_out), .b(32'h1), .out(LowC2), .cout(adder_1_cout));  // open: cin
  assign not_2_out = ~High;  // NOT_Gate not_2, 32 bits wide
  Adder #(.width(32)) adder_2 (.a(not_2_out), .b({32{1'b0}}), .out(HighC2), .cin(adder_1_cout));  // open: cout
endmodule
